// Logisim project DMA_Project.circ as structural Verilog: 5 circuits, main circuit main
module main (
  input  [31:0] Address,
  input  [31:0] Data,
  input  WR,
  input  RD,
  input  in_5,
  input  [1:0] BW,
  output [31:0] out_7
);

  wire adecoder_1_csdisp, adecoder_1_csdma, adecoder_1_csmem, and_1_out, and_2_out, and_3_out, button_1_out,
       button_2_out, clock_1_out, controlled_buffer_3_out, controlled_buffer_4_out, dma_1_hold,
       memadapter_1_clk, memadapter_1_oe, memadapter_1_we, not_1_out, or_1_out;
  wire [1:0] controlled_buffer_5_out;
  wire [15:0] memadapter_1_mema;
  wire [31:0] controlled_buffer_1_out, memadapter_1_memdo, ram_1_dout, register_1_q;

  Clock clock_1 (.out(clock_1_out));
  Button button_1 (.out(button_1_out));
  Button button_2 (.out(button_2_out));
  or or_1 (or_1_out, clock_1_out, button_1_out);
  assign controlled_buffer_1_out = not_1_out ? Address : 32'bz;  // Controlled_Buffer controlled_buffer_1
  assign out_7 = and_1_out ? Data : 32'bz;  // Controlled_Buffer controlled_buffer_2
  and and_1 (and_1_out, WR, not_1_out);
  assign controlled_buffer_3_out = not_1_out ? WR : 1'bz;  // Controlled_Buffer controlled_buffer_3
  assign controlled_buffer_4_out = not_1_out ? RD : 1'bz;  // Controlled_Buffer controlled_buffer_4
  not not_1 (not_1_out, dma_1_hold);
  assign controlled_buffer_5_out = not_1_out ? BW : 2'bz;  // Controlled_Buffer controlled_buffer_5
  and and_2 (and_2_out, controlled_buffer_3_out, adecoder_1_csdisp);
  and and_3 (and_3_out, controlled_buffer_4_out, adecoder_1_csdisp);
  DMA dma_1 (
    .Ao(controlled_buffer_1_out), .Do(out_7), .WRo(controlled_buffer_3_out), .RDo(controlled_buffer_4_out),
    .HOLD(dma_1_hold), .BW(controlled_buffer_5_out), .Ai(controlled_buffer_1_out), .Di(out_7),
    .WRi(controlled_buffer_3_out), .RDi(controlled_buffer_4_out), .CS(adecoder_1_csdma), .CLK(or_1_out),
    .RST(button_2_out));  // open: INT
  MemAdapter memadapter_1 (
    .WE(memadapter_1_we), .OE(memadapter_1_oe), .clk(memadapter_1_clk), .BusDo(out_7),
    .MemA(memadapter_1_mema), .MemDo(memadapter_1_memdo), .in_1(1'b0), .WR(controlled_buffer_3_out),
    .CS(adecoder_1_csmem), .RD(controlled_buffer_4_out), .Clock(or_1_out),
    .ByteA(controlled_buffer_1_out[17:0]), .Width(controlled_buffer_5_out), .BusDi(out_7), .MemDi(ram_1_dout));  // open: AddrError
  assign out_7 = and_3_out ? register_1_q : 32'bz;  // Controlled_Buffer controlled_buffer_6
  ADecoder adecoder_1 (
    .CSMem(adecoder_1_csmem), .CSDMA(adecoder_1_csdma), .CSDisp(adecoder_1_csdisp),
    .Address(controlled_buffer_1_out));
  RAM #(.addrWidth(16), .asyncread("true"), .dataWidth(32), .\type ("nonvolatile")) ram_1 (
    .addr(memadapter_1_mema), .we(memadapter_1_we), .oe(memadapter_1_oe), .clk(memadapter_1_clk),
    .din(memadapter_1_memdo), .dout(ram_1_dout));
  Register register_1 (.D(out_7[7:0]), .en(and_2_out), .clk(or_1_out), .Q(register_1_q[7:0]), .clr(button_2_out));
  Pull_Resistor pull_resistor_1 (.node(register_1_q[31:8]));
  Hex_Digit_Display hex_digit_display_1 (.value(register_1_q[7:4]));  // open: dp
  Hex_Digit_Display hex_digit_display_2 (.value(register_1_q[3:0]));  // open: dp

  // Notes on the sheet:
  //   0000 0000 - FFFF 0000
endmodule

module DMA (
  input  [31:0] Ai,
  input  [31:0] Di,
  input  WRi,
  input  RDi,
  input  CS,
  input  CLK,
  input  RST,
  output [31:0] Ao,
  output [31:0] Do,
  output WRo,
  output RDo,
  output HOLD,
  output INT,
  output [1:0] BW
);

  wire and_3_out, and_4_out, and_5_out, and_6_out, and_7_out, and_8_out, and_9_out, and_10_out, and_11_out,
       and_12_out, and_13_out, and_14_out, and_15_out, and_16_out, and_17_out, and_18_out, and_19_out,
       and_20_out, counter_1_q, FIM, MD, MO, or_1_out, or_2_out, or_3_out, or_4_out, rC, RD, rD_t, RDY, rN,
       rO, t0, t1, WR;
  wire [1:0] WB;
  wire [6:0] Estado_q;
  wire [6:4] Controle_q;
  wire [31:0] Dado_q, Destino_q, incrementa_1_ao, multiplexer_1_out, Origem_q, register_2_q;

  and and_1 (WR, CS, WRi);
  and and_2 (RD, CS, RDi);
  Decoder #(.select(2)) decoder_1 (.out0(rO), .out1(rD_t), .out2(rN), .out3(rC), .sel(Ai[1:0]), .en(CS));
  Decoder decoder_2 (.out0(t0), .out1(t1), .sel(counter_1_q));  // open: en
  Counter #(.max('h1), .width(1)) counter_1 (
    .load(1'b0), .count(1'b1), .Q(counter_1_q), .up(1'b1), .clk(CLK), .clr(or_1_out));  // open: D, carry
  or or_1 (or_1_out, RST, ~HOLD);  // OR_Gate
  Register #(.trigger("high"), .width(32)) Dado (.D(Di), .en(HOLD), .clk(t0), .Q(Dado_q), .clr(RST));
  Register Controle (.D(Di[7:0]), .en(and_3_out), .clk(CLK), .Q({HOLD, Controle_q, BW, MD, MO}), .clr(or_2_out));
  and and_3 (and_3_out, rC, WR);
  and and_4 (and_4_out, HOLD, RDY);
  and and_5 (and_5_out, rO, WR);
  and and_6 (and_6_out, MO, t1);
  assign WRo = and_7_out ? 1'b0 : 1'bz;  // Controlled_Buffer controlled_buffer_1
  assign RDo = and_7_out ? 1'b1 : 1'bz;  // Controlled_Buffer controlled_buffer_2
  and and_7 (and_7_out, HOLD, t0);
  or or_2 (or_2_out, RST, and_4_out);
  Counter #(.max('hffffffff), .width(32)) Origem (
    .load(and_5_out), .D(Di), .count(and_6_out), .Q(Origem_q), .up(1'b1), .clk(CLK), .clr(RST));  // open: carry
  and and_8 (and_8_out, HOLD, t0);
  and and_9 (and_9_out, t1, HOLD);
  Register register_1 (.D({HOLD, Controle_q, BW, MD, MO}), .en(1'b1), .clk(CLK), .clr(or_2_out));  // open: Q
  assign Ao = and_8_out ? Origem_q : 32'bz;  // Controlled_Buffer controlled_buffer_3
  assign Do = and_9_out ? Dado_q : 32'bz;  // Controlled_Buffer controlled_buffer_4
  and and_10 (and_10_out, rD_t, WR);
  and and_11 (and_11_out, MD, t1);
  and and_12 (and_12_out, HOLD, t1);
  and and_13 (and_13_out, rO, WR);
  and and_14 (and_14_out, MO, t1);
  Counter #(.max('hffffffff), .width(32)) Destino (
    .load(and_10_out), .D(Di), .count(and_11_out), .Q(Destino_q), .up(1'b1), .clk(CLK), .clr(RST));  // open: carry
  assign RDo = and_12_out ? 1'b0 : 1'bz;  // Controlled_Buffer controlled_buffer_5
  assign WRo = and_12_out ? 1'b1 : 1'bz;  // Controlled_Buffer controlled_buffer_6
  Register #(.width(32)) register_2 (.D(multiplexer_1_out), .en(or_3_out), .clk(CLK), .Q(register_2_q), .clr(RST));
  Multiplexer #(.width(32)) multiplexer_1 (.in0(incrementa_1_ao), .in1(Di), .out(multiplexer_1_out), .sel(and_13_out));
  or or_3 (or_3_out, and_13_out, and_14_out);
  assign Ao = and_15_out ? Destino_q : 32'bz;  // Controlled_Buffer controlled_buffer_7
  and and_15 (and_15_out, HOLD, t1);
  and and_16 (and_16_out, HOLD, ~FIM);  // AND_Gate
  Incrementa incrementa_1 (.Ao(incrementa_1_ao), .Ai(register_2_q), .BW(BW));
  assign Ao = and_17_out ? register_2_q : 32'bz;  // Controlled_Buffer controlled_buffer_8
  and and_17 (and_17_out, HOLD, t0);
  Register Estado (.D({FIM, {7{1'b0}}}), .en(1'b1), .clk(CLK), .Q({RDY, Estado_q}), .clr(or_4_out));
  or or_4 (or_4_out, RST, and_16_out);
  and and_18 (and_18_out, rN, WR);
  and and_19 (and_19_out, HOLD, t1);
  assign WB = HOLD ? WB : 2'bz;  // Controlled_Buffer controlled_buffer_9
  and and_20 (and_20_out, rC, RD);
  Counter #(.max('hffffffff), .ongoal("stay"), .width(32)) NBytes (
    .load(and_18_out), .D(Di), .count(and_19_out), .carry(FIM), .up(1'b0), .clk(CLK), .clr(RST));  // open: Q
  assign Do = and_20_out ? {{24{1'b0}}, RDY, Estado_q} : 32'bz;  // Controlled_Buffer controlled_buffer_10

  // Other names for the same wires on the sheet: GO = HOLD; BYTEi[7:0] = Di[7:0]

  // Notes on the sheet:
  //   Do: pull=down
endmodule

module MemAdapter (
  input  in_1,
  input  WR,
  input  CS,
  input  RD,
  input  Clock,
  input  [31:0] BusDi,
  input  [1:0] Width,
  input  [31:0] MemDi,
  input  [17:0] ByteA,
  output WE,
  output OE,
  output clk,
  output [31:0] BusDo,
  output AddrError,
  output [15:0] MemA,
  output [31:0] MemDo
);

  wire and_3_out, and_8_out, and_9_out, and_10_out, and_11_out, not_1_out, not_2_out, not_3_out;
  wire [31:0] and_4_out, and_5_out, and_6_out, and_7_out, BusDo_t, MemDi_t, multiplexer_1_out, ram_1_dout,
       shifter_1_out, shifter_2_out, shifter_3_out, xor_1_out;

  not not_1 (not_1_out, AddrError);
  Multiplexer #(.enable("true"), .select(2), .width(32)) multiplexer_1 (
    .in0({32{1'b1}}), .in1(32'hffff), .in2(32'hff), .in3({32{1'b0}}), .out(multiplexer_1_out), .sel(Width),
    .en(not_1_out));
  and and_1 (WE, WR, CS);
  and and_2 (OE, CS, RD);
  and and_3 (and_3_out, CS, RD, ~AddrError);  // AND_Gate
  assign MemDi_t = not_2_out ? MemDi : 32'bz;  // Controlled_Buffer controlled_buffer_1
  assign BusDo = and_3_out ? BusDo_t : 32'bz;  // Controlled_Buffer controlled_buffer_2
  not not_2 (not_2_out, in_1);
  Shifter #(.width(32)) shifter_1 (.in(multiplexer_1_out), .\dist ({ByteA[1:0], 3'b000}), .out(shifter_1_out));
  Shifter #(.width(32)) shifter_2 (.in(BusDi), .\dist ({ByteA[1:0], 3'b000}), .out(shifter_2_out));
  assign xor_1_out = {32{1'b1}} ^ shifter_1_out;  // XOR_Gate xor_1, 32 bits wide
  assign and_4_out = xor_1_out & MemDi_t;  // AND_Gate and_4, 32 bits wide
  assign and_5_out = shifter_1_out & shifter_2_out;  // AND_Gate and_5, 32 bits wide
  assign MemDo = and_4_out | and_5_out;  // OR_Gate or_1, 32 bits wide
  RAM #(.addrWidth(16), .asyncread("true"), .dataWidth(32), .\type ("nonvolatile")) ram_1 (
    .addr(ByteA[17:2]), .we(WE), .oe(OE), .clk(Clock), .din(MemDi_t), .dout(ram_1_dout));
  Shifter #(.shift("lr"), .width(32)) shifter_3 (.in(MemDi_t), .\dist ({ByteA[1:0], 3'b000}), .out(shifter_3_out));
  assign and_6_out = shifter_3_out & 32'hffff;  // AND_Gate and_6, 32 bits wide
  assign and_7_out = shifter_3_out & 32'hff;  // AND_Gate and_7, 32 bits wide
  and and_8 (and_8_out, Width[1], Width[0]);
  and and_9 (and_9_out, ByteA[0], ~Width[1], ~Width[0]);  // AND_Gate
  and and_10 (and_10_out, ByteA[1], ~Width[1], ~Width[0]);  // AND_Gate
  and and_11 (and_11_out, ByteA[1], ByteA[0], ~Width[1]);  // AND_Gate
  not not_3 (not_3_out, AddrError);
  Multiplexer #(.enable("true"), .select(2), .width(32)) multiplexer_2 (
    .in0(MemDi_t), .in1(and_6_out), .in2(and_7_out), .out(BusDo_t), .sel(Width), .en(not_3_out));  // open: in3
  or or_2 (AddrError, and_8_out, and_9_out, and_10_out, and_11_out);
  assign MemDi_t = in_1 ? ram_1_dout : 32'bz;  // Controlled_Buffer controlled_buffer_3

  assign clk = Clock;
  assign MemA = ByteA[17:2];

  // Other names for the same wires on the sheet: LSb[1:0] = ByteA[1:0]; AlignErr = AddrError; A[15:0] = ByteA[17:2];
  //   DWidth[1:0] = Width; Teste = in_1
endmodule

module ADecoder (
  input  [31:0] Address,
  output CSMem,
  output CSDMA,
  output CSDisp
);

  wire and_1_out, comparator_1_eq, comparator_1_lt, comparator_2_eq, comparator_2_gt;

  Comparator #(.mode("unsigned"), .width(32)) comparator_1 (
    .a(Address), .b(32'h3ffff), .eq(comparator_1_eq), .lt(comparator_1_lt));  // open: gt
  Comparator #(.mode("unsigned"), .width(32)) comparator_2 (
    .a(Address), .b(32'hfffffff0), .gt(comparator_2_gt), .eq(comparator_2_eq));  // open: lt
  Comparator #(.mode("unsigned"), .width(32)) comparator_3 (
    .a(Address), .b(32'hffff0000), .eq(CSDisp));  // open: gt, lt
  or or_1 (CSMem, comparator_1_eq, comparator_1_lt);
  or or_2 (CSDMA, comparator_2_gt, comparator_2_eq);
  and and_1 (and_1_out, Address[0], Address[1], Address[2], Address[3], Address[4], Address[5], Address[6], Address[7], Address[8], Address[9], Address[10], Address[11], Address[12], Address[13], Address[14], Address[15], ~Address[16], ~Address[17], ~Address[18], ~Address[19], ~Address[20], ~Address[21], ~Address[22], ~Address[23], ~Address[24], ~Address[25], ~Address[26], ~Address[27], ~Address[28], ~Address[29], ~Address[30], ~Address[31]);  // AND_Gate
endmodule

module Incrementa (
  input  [31:0] Ai,
  input  [1:0] BW,
  output [31:0] Ao
);

  wire [1:0] subtractor_1_out;
  wire [4:0] bit_extender_1_out;
  wire [31:0] adder_1_out, shifter_1_out;

  Subtractor #(.width(2)) subtractor_1 (.a(2'b10), .b(BW), .out(subtractor_1_out));  // open: bin, bout
  assign bit_extender_1_out = {{3{1'b0}}, subtractor_1_out};  // Bit_Extender bit_extender_1
  Shifter #(.shift("lr"), .width(32)) shifter_1 (.in(Ai), .\dist (bit_extender_1_out), .out(shifter_1_out));
  Adder #(.width(32)) adder_1 (.a(32'h1), .b(shifter_1_out), .out(adder_1_out));  // open: cin, cout
  Shifter #(.width(32)) shifter_2 (.in(adder_1_out), .\dist (bit_extender_1_out), .out(Ao));
endmodule
