// Logisim project ProtoOne.v0.1.circ as structural Verilog: 9 circuits, main circuit main
module main (
  input  in_1,
  input  in_2,
  input  in_3,
  input  in_4,
  input  in_5,
  input  in_6,
  input  in_7,
  input  in_8,
  input  in_9,
  input  in_10,
  input  in_11,
  input  [2:0] in_12
);

  wire button_1_out, Clk, clock_1_out, d_ff_1_q, decoder_1_out0, decoder_1_out1, decoder_1_out2,
       decoder_1_out3, decoder_1_out4, por_1_out;
  wire [3:0] memio_1_memcontrol;
  wire [3:3] CtrlBus;
  wire [7:0] acc_1_accout, mar_1_marout, mdr_1_dataout, mdr_1_dbusout, multiplexer_1_out, pc_1_pcout,
       ula_1_flags, ula_1_ulaout;

  Clock clock_1 (.out(clock_1_out));
  Button button_1 (.out(button_1_out));
  PC pc_1 (.PCload(in_2), .PCinc(in_1), .CLKin(Clk), .Reset(CtrlBus[3]), .PCin(mdr_1_dataout), .PCout(pc_1_pcout));
  MAR mar_1 (.MARIn(mdr_1_dataout), .MARload(in_5), .ClkIn(Clk), .Reset(CtrlBus[3]), .MAROut(mar_1_marout));
  ACC acc_1 (.AccIn(ula_1_ulaout), .ACCload(in_3), .ClkIn(Clk), .Reset(CtrlBus[3]), .AccOut(acc_1_accout));
  POR por_1 (.out(por_1_out));
  D_Flip_Flop d_ff_1 (.D(1'b1), .clk(clock_1_out), .Q(d_ff_1_q), .reset(CtrlBus[3]));  // open: Qn, preset
  or or_1 (CtrlBus[3], por_1_out, button_1_out);
  Multiplexer #(.width(8)) multiplexer_1 (.in0(pc_1_pcout), .in1(mar_1_marout), .out(multiplexer_1_out), .sel(in_10));
  ULA ula_1 (.Y(mdr_1_dataout), .ULAoper(in_12), .X(acc_1_accout), .Flags(ula_1_flags), .ULAout(ula_1_ulaout));
  and and_1 (Clk, ~in_11, clock_1_out, d_ff_1_q);  // AND_Gate
  MDR mdr_1 (
    .MEMread(in_8), .MDRload(in_4), .Clk(Clk), .Rst(CtrlBus[3]), .MEMwrite(in_9), .DataIn(acc_1_accout),
    .DBusIn(mdr_1_dbusout), .DataOut(mdr_1_dataout), .DBusOut(mdr_1_dbusout));
  IR ir_1 (.IRload(in_6), .ClkIn(Clk), .IRIn(mdr_1_dbusout), .Reset(CtrlBus[3]));  // open: IROut
  Flags flags_1 (.FlagsIn(ula_1_flags), .FLAGSload(in_7), .Clk(Clk), .Reset(CtrlBus[3]));  // open: FlagsOut
  MemIO memio_1 (
    .Control({CtrlBus[3], Clk, in_8, in_9}), .Address(multiplexer_1_out), .MemControl(memio_1_memcontrol));  // open: IOControl, P0, P1, P2, P3, P4, P5, P6, P7
  RAM #(.asyncread("true"), .databus("bidir"), .\type ("nonvolatile")) Memoria (
    .addr(multiplexer_1_out), .we(memio_1_memcontrol[0]), .oe(memio_1_memcontrol[1]),
    .clk(memio_1_memcontrol[2]), .data(mdr_1_dbusout));
  Decoder #(.enable("false"), .select(3)) decoder_1 (
    .out0(decoder_1_out0), .out1(decoder_1_out1), .out2(decoder_1_out2), .out3(decoder_1_out3),
    .out4(decoder_1_out4), .sel(in_12));  // open: out5, out6, out7
  LED ADDoper (.in(decoder_1_out0));
  LED ANDoper (.in(decoder_1_out1));
  LED ORoper (.in(decoder_1_out2));
  LED NOToper (.in(decoder_1_out3));
  LED Yoper (.in(decoder_1_out4));

  // Other names for the same wires on the sheet: ACCload = in_3; ADDRsel = in_10; CtrlBus[2:0] = {Clk, in_8, in_9};
  //   MEMwrite = in_9; MEMread = in_8; Rst = CtrlBus[3]; FLAGSload = in_7; Halt = in_11; IRload = in_6;
  //   MARload = in_5; MDRload = in_4; PCinc = in_1; PCload = in_2; ULAoper[2:0] = in_12

  // Notes on the sheet:
  //   Barramento
  //   Dados
  //   Endereços
  //   Controle
endmodule

module ULA (
  input  [7:0] X,
  input  [7:0] Y,
  input  [2:0] ULAoper,
  output [7:0] Flags,
  output [7:0] ULAout
);

  wire [7:0] adder_1_out, and_1_out, not_1_out, or_1_out;

  assign not_1_out = ~X;  // NOT_Gate not_1, 8 bits wide
  Adder adder_1 (.a(Y), .b(X), .out(adder_1_out), .cin(1'b0), .cout(Flags[2]));
  assign and_1_out = Y & X;  // AND_Gate and_1, 8 bits wide
  assign or_1_out = Y | X;  // OR_Gate or_1, 8 bits wide
  Multiplexer #(.select(3), .width(8)) multiplexer_1 (
    .in0(adder_1_out), .in1(and_1_out), .in2(or_1_out), .in3(not_1_out), .in4(Y),
    .out({Flags[1], ULAout[6:0]}), .sel(ULAoper));  // open: in5, in6, in7
  nor nor_1 (Flags[0], ULAout[0], ULAout[1], ULAout[2], ULAout[3], ULAout[4], ULAout[5], ULAout[6], Flags[1]);

  assign ULAout[7] = Flags[1];
endmodule

module PC (
  input  [7:0] PCin,
  input  PCload,
  input  PCinc,
  input  CLKin,
  input  Reset,
  output [7:0] PCout
);

  wire or_1_out;
  wire [7:0] adder_1_out, multiplexer_1_out;

  or or_1 (or_1_out, PCload, PCinc);
  Multiplexer #(.width(8)) multiplexer_1 (.in0(PCin), .in1(adder_1_out), .out(multiplexer_1_out), .sel(PCinc));
  Register register_1 (.D(multiplexer_1_out), .en(or_1_out), .clk(CLKin), .Q(PCout), .clr(Reset));
  Adder adder_1 (.a(PCout), .b(8'h1), .out(adder_1_out), .cin(1'b0));  // open: cout
endmodule

module MDR (
  input  [7:0] DataIn,
  input  [7:0] DBusIn,
  input  MEMread,
  input  MDRload,
  input  Clk,
  input  Rst,
  input  MEMwrite,
  output [7:0] DBusOut,
  output [7:0] DataOut
);

  wire [7:0] multiplexer_1_out;

  Register register_1 (.D(multiplexer_1_out), .en(MDRload), .clk(Clk), .Q(DataOut), .clr(Rst));
  Multiplexer #(.width(8)) multiplexer_1 (.in0(DataIn), .in1(DBusIn), .out(multiplexer_1_out), .sel(MEMread));
  assign DBusOut = MEMwrite ? DataOut : 8'bz;  // Controlled_Buffer controlled_buffer_1
endmodule

module MAR (
  input  [7:0] MARIn,
  input  MARload,
  input  ClkIn,
  input  Reset,
  output [7:0] MAROut
);

  Register register_1 (.D(MARIn), .en(MARload), .clk(ClkIn), .Q(MAROut), .clr(Reset));
endmodule

module ACC (
  input  [7:0] AccIn,
  input  ACCload,
  input  ClkIn,
  input  Reset,
  output [7:0] AccOut
);

  Register register_1 (.D(AccIn), .en(ACCload), .clk(ClkIn), .Q(AccOut), .clr(Reset));
endmodule

module IR (
  input  [7:0] IRIn,
  input  IRload,
  input  ClkIn,
  input  Reset,
  output [7:0] IROut
);

  Register register_1 (.D(IRIn), .en(IRload), .clk(ClkIn), .Q(IROut), .clr(Reset));
endmodule

module Flags (
  input  [7:0] FlagsIn,
  input  FLAGSload,
  input  Clk,
  input  Reset,
  output [7:0] FlagsOut
);

  Register Flags (.D(FlagsIn), .en(FLAGSload), .clk(Clk), .Q(FlagsOut), .clr(Reset));
  LED C (.in(FlagsOut[2]));
  LED N (.in(FlagsOut[1]));
  LED Z (.in(FlagsOut[0]));
endmodule

module MemIO (
  input  [3:0] Control,
  input  [7:0] Address,
  output [3:0] MemControl,
  output [3:0] IOControl,
  output P0,
  output P1,
  output P2,
  output P3,
  output P4,
  output P5,
  output P6,
  output P7
);

  wire [3:3] and_1_out;

  and and_1 (and_1_out[3], Address[7], Address[6], Address[5], Address[4], Address[3]);
  Decoder #(.select(3)) decoder_1 (
    .out0(P0), .out1(P1), .out2(P2), .out3(P3), .out4(P4), .out5(P5), .out6(P6), .out7(P7),
    .sel(Address[2:0]), .en(and_1_out[3]));
  assign MemControl = Control & ~{4{and_1_out[3]}};  // AND_Gate and_2, 4 bits wide
  assign IOControl = Control & {4{and_1_out[3]}};  // AND_Gate and_3, 4 bits wide
endmodule
