// Logisim project ProtoOne.v1.1.circ as structural Verilog: 11 circuits, main circuit main
module main (
);

  wire ACCload, ADDRsel, button_1_out, Clk, clock_1_out, d_ff_1_q, FLAGSload, Halt, IRload, MARload, MDRload,
       PCinc, PCload, por_1_out;
  wire [2:0] ULAoper;
  wire [3:0] CtrlBus, memio_1_memcontrol;
  wire [7:0] acc_1_accout, flags_1_flagsout, ir_1_irout, mar_1_marout, mdr_1_dataout, mdr_1_dbusout,
       multiplexer_1_out, pc_1_pcout, ula_1_flags, ula_1_ulaout;

  Clock clock_1 (.out(clock_1_out));
  Button button_1 (.out(button_1_out));
  PC pc_1 (.PCload(PCload), .PCinc(PCinc), .CLKin(Clk), .Reset(CtrlBus[3]), .PCin(mdr_1_dataout), .PCout(pc_1_pcout));
  MAR mar_1 (.MARIn(mdr_1_dataout), .MARload(MARload), .ClkIn(Clk), .Reset(CtrlBus[3]), .MAROut(mar_1_marout));
  ACC acc_1 (.ACCload(ACCload), .AccIn(ula_1_ulaout), .ClkIn(Clk), .Reset(CtrlBus[3]), .AccOut(acc_1_accout));
  POR por_1 (.out(por_1_out));
  D_Flip_Flop d_ff_1 (.D(1'b1), .clk(clock_1_out), .Q(d_ff_1_q), .reset(CtrlBus[3]));  // open: Qn, preset
  or or_1 (CtrlBus[3], por_1_out, button_1_out);
  Multiplexer #(.width(8)) multiplexer_1 (.in0(pc_1_pcout), .in1(mar_1_marout), .out(multiplexer_1_out), .sel(ADDRsel));
  ULA ula_1 (.Y(mdr_1_dataout), .X(acc_1_accout), .ULAoper(ULAoper), .Flags(ula_1_flags), .ULAout(ula_1_ulaout));
  and and_1 (Clk, clock_1_out, d_ff_1_q);
  IDecoder idecoder_1 (
    .Reset(CtrlBus[3]), .Clk(Clk), .Din(ir_1_irout), .Flags(flags_1_flagsout), .ULAoper(ULAoper),
    .PCload(PCload), .ACCload(ACCload), .MDRload(MDRload), .MARload(MARload), .IRload(IRload),
    .FLAGSload(FLAGSload), .MEMread(CtrlBus[1]), .MEMwrite(CtrlBus[0]), .ADDRsel(ADDRsel), .Halt(Halt),
    .PCinc(PCinc));
  MDR mdr_1 (
    .MDRload(MDRload), .Clk(Clk), .Rst(CtrlBus[3]), .MEMwrite(CtrlBus[0]), .MEMread(CtrlBus[1]),
    .DataIn(acc_1_accout), .DBusIn(mdr_1_dbusout), .DataOut(mdr_1_dataout), .DBusOut(mdr_1_dbusout));
  IR ir_1 (.IRIn(mdr_1_dbusout), .IRload(IRload), .ClkIn(Clk), .Reset(CtrlBus[3]), .IROut(ir_1_irout));
  Flags flags_1 (
    .Clk(Clk), .Reset(CtrlBus[3]), .FlagsIn(ula_1_flags), .FLAGSload(FLAGSload), .FlagsOut(flags_1_flagsout));
  MemIO memio_1 (
    .Control({CtrlBus[3], Clk, CtrlBus[1:0]}), .Address(multiplexer_1_out), .MemControl(memio_1_memcontrol));  // open: IOControl, P0, P1, P2, P3, P4, P5, P6, P7
  RAM #(.asyncread("true"), .databus("bidir"), .\type ("nonvolatile")) Memoria (
    .addr(multiplexer_1_out), .we(memio_1_memcontrol[0]), .oe(memio_1_memcontrol[1]),
    .clk(memio_1_memcontrol[2]), .data(mdr_1_dbusout));

  // Other names for the same wires on the sheet: MEMwrite = CtrlBus[0]; MEMread = CtrlBus[1]; CtrlBus[2] = Clk;
  //   Rst = CtrlBus[3]

  // Notes on the sheet:
  //   Barramento
  //   Dados
  //   Endereços
  //   Controle
endmodule

module ULA (
  input  [7:0] X,
  input  [7:0] Y,
  input  [2:0] ULAoper,
  output [7:0] Flags,
  output [7:0] ULAout
);

  wire [7:0] adder_1_out, and_1_out, not_1_out, or_1_out;

  Adder adder_1 (.a(Y), .b(X), .out(adder_1_out), .cin(1'b0), .cout(Flags[2]));
  assign and_1_out = Y & X;  // AND_Gate and_1, 8 bits wide
  assign or_1_out = Y | X;  // OR_Gate or_1, 8 bits wide
  assign not_1_out = ~X;  // NOT_Gate not_1, 8 bits wide
  Multiplexer #(.select(3), .width(8)) multiplexer_1 (
    .in0(adder_1_out), .in1(and_1_out), .in2(or_1_out), .in3(not_1_out), .in4(Y),
    .out({Flags[1], ULAout[6:0]}), .sel(ULAoper));  // open: in5, in6, in7
  nor nor_1 (Flags[0], ULAout[0], ULAout[1], ULAout[2], ULAout[3], ULAout[4], ULAout[5], ULAout[6], Flags[1]);

  assign ULAout[7] = Flags[1];
endmodule

module IDecoder (
  input  [7:0] Flags,
  input  [7:0] Din,
  input  Reset,
  input  Clk,
  output [2:0] ULAoper,
  output PCinc,
  output PCload,
  output ACCload,
  output MDRload,
  output MARload,
  output IRload,
  output FLAGSload,
  output MEMread,
  output MEMwrite,
  output ADDRsel,
  output Halt
);

  wire and_1_out, and_2_out, and_4_out, and_5_out, and_8_out, and_9_out, and_10_out, and_11_out, and_12_out,
       and_13_out, and_14_out, and_15_out, and_16_out, and_17_out, and_18_out, iADD, iAND, iHLT, iJMP, iJN,
       iJZ, iLDA, iNOP, iNOT, iOR, iSTA, nor_1_out, nor_2_out, nor_3_out, or_1_out, or_3_out, or_5_out,
       or_6_out, or_7_out, or_11_out, T1, T2, T3, T4, T5, T6, T7;
  wire [2:0] counter_1_q;

  Counter #(.max('h7), .width(3)) counter_1 (
    .clr(Reset), .load(1'b0), .up(1'b1), .count(1'b1), .clk(and_1_out), .Q(counter_1_q));  // open: D, carry
  and and_1 (and_1_out, ~Clk, ~Halt);  // AND_Gate
  and and_2 (and_2_out, T3, nor_1_out);
  nor nor_1 (nor_1_out, iNOP, iNOT, iHLT);
  or or_1 (or_1_out, iSTA, iLDA, iADD, iAND, iOR);
  and and_3 (MARload, or_1_out, T3);
  Decoder #(.select(4)) decoder_1 (
    .out0(iNOP), .out1(iSTA), .out2(iLDA), .out3(iADD), .out4(iOR), .out5(iAND), .out6(iNOT), .out8(iJMP),
    .out9(iJN), .out10(iJZ), .out15(iHLT), .sel(Din[7:4]), .en(1'b1));  // open: out7, out11, out12, out13, out14
  or or_2 (PCinc, T1, and_2_out);
  Decoder #(.enable("false"), .select(3)) decoder_2 (
    .out0(IRload), .out1(T1), .out2(T2), .out3(T3), .out4(T4), .out5(T5), .out6(T6), .out7(T7),
    .sel(counter_1_q));
  or or_3 (or_3_out, iADD, iAND, iOR, iLDA);
  and and_4 (and_4_out, iNOT, T2);
  and and_5 (and_5_out, or_3_out, T5);
  or or_4 (ACCload, and_5_out, and_4_out);
  and and_6 (Halt, iHLT, T1);
  and and_7 (MEMwrite, T5, iSTA);
  or or_5 (or_5_out, iLDA, iADD, iOR, iAND);
  or or_6 (or_6_out, iADD, iAND, iOR);
  and and_8 (and_8_out, iNOT, T3);
  nor nor_2 (nor_2_out, iNOP, iNOT, iHLT);
  or or_7 (or_7_out, iLDA, iADD, iOR, iAND);
  and and_9 (and_9_out, or_5_out, T4);
  or or_8 (ADDRsel, and_9_out, and_10_out);
  and and_10 (and_10_out, iSTA, T5);
  and and_11 (and_11_out, or_6_out, T6);
  or or_9 (FLAGSload, and_11_out, and_8_out);
  and and_12 (and_12_out, T2, nor_2_out);
  or or_10 (MEMread, IRload, and_12_out, and_13_out);
  and and_13 (and_13_out, T4, or_7_out);
  ULAdecoder uladecoder_1 (
    .iANDin(iAND), .iADDin(iNOT), .iNOTin(iADD), .T2(T2), .iORin(iOR), .T5(T5), .iLDAin(iLDA),
    .operation(ULAoper));
  nor nor_3 (nor_3_out, iNOP, iNOT, iHLT);
  or or_11 (or_11_out, iLDA, iSTA, iADD, iOR, iAND);
  and and_14 (and_14_out, iJMP, T4);
  and and_15 (and_15_out, Flags[1], T4, iJN);
  and and_16 (and_16_out, Flags[0], T4, iJZ);
  and and_17 (and_17_out, T2, nor_3_out);
  or or_12 (MDRload, and_17_out, and_18_out);
  and and_18 (and_18_out, or_11_out, T4);
  or or_13 (PCload, and_14_out, and_15_out, and_16_out);

  // Other names for the same wires on the sheet: Zin = Flags[0]; Nin = Flags[1]; Cin = Flags[2]; T0 = IRload
endmodule

module ULAdecoder (
  input  iLDAin,
  input  iANDin,
  input  iADDin,
  input  iNOTin,
  input  T2,
  input  iORin,
  input  T5,
  output [2:0] operation
);

  wire and_2_out, and_3_out, and_4_out, and_5_out;

  and and_1 (operation[2], T5, iLDAin);
  and and_2 (and_2_out, iNOTin, T2);
  and and_3 (and_3_out, iANDin, T5);
  and and_4 (and_4_out, iNOTin, T2);
  and and_5 (and_5_out, iORin, T5);
  or or_1 (operation[1], and_2_out, and_3_out);
  or or_2 (operation[0], and_4_out, and_5_out);
endmodule

module PC (
  input  [7:0] PCin,
  input  PCload,
  input  PCinc,
  input  CLKin,
  input  Reset,
  output [7:0] PCout
);

  wire or_1_out;
  wire [7:0] adder_1_out, multiplexer_1_out;

  or or_1 (or_1_out, PCload, PCinc);
  Multiplexer #(.width(8)) multiplexer_1 (.in0(PCin), .in1(adder_1_out), .out(multiplexer_1_out), .sel(PCinc));
  Register register_1 (.D(multiplexer_1_out), .en(or_1_out), .clk(CLKin), .Q(PCout), .clr(Reset));
  Adder adder_1 (.a(PCout), .b(8'h1), .out(adder_1_out), .cin(1'b0));  // open: cout
endmodule

module MDR (
  input  [7:0] DataIn,
  input  [7:0] DBusIn,
  input  MEMread,
  input  MDRload,
  input  Clk,
  input  Rst,
  input  MEMwrite,
  output [7:0] DBusOut,
  output [7:0] DataOut
);

  wire [7:0] multiplexer_1_out;

  Register register_1 (.D(multiplexer_1_out), .en(MDRload), .clk(Clk), .Q(DataOut), .clr(Rst));
  Multiplexer #(.width(8)) multiplexer_1 (.in0(DataIn), .in1(DBusIn), .out(multiplexer_1_out), .sel(MEMread));
  assign DBusOut = MEMwrite ? DataOut : 8'bz;  // Controlled_Buffer controlled_buffer_1
endmodule

module MAR (
  input  [7:0] MARIn,
  input  MARload,
  input  ClkIn,
  input  Reset,
  output [7:0] MAROut
);

  Register register_1 (.D(MARIn), .en(MARload), .clk(ClkIn), .Q(MAROut), .clr(Reset));
endmodule

module ACC (
  input  [7:0] AccIn,
  input  ACCload,
  input  ClkIn,
  input  Reset,
  output [7:0] AccOut
);

  Register AC (.D(AccIn), .en(ACCload), .clk(ClkIn), .Q(AccOut), .clr(Reset));
endmodule

module IR (
  input  [7:0] IRIn,
  input  IRload,
  input  ClkIn,
  input  Reset,
  output [7:0] IROut
);

  Register register_1 (.D(IRIn), .en(IRload), .clk(ClkIn), .Q(IROut), .clr(Reset));
endmodule

module Flags (
  input  [7:0] FlagsIn,
  input  FLAGSload,
  input  Clk,
  input  Reset,
  output [7:0] FlagsOut
);

  Register Flags (.D(FlagsIn), .en(FLAGSload), .clk(Clk), .Q(FlagsOut), .clr(Reset));
  LED led_1 (.in(FlagsOut[2]));
  LED led_2 (.in(FlagsOut[1]));
  LED led_3 (.in(FlagsOut[0]));
endmodule

module MemIO (
  input  [3:0] Control,
  input  [7:0] Address,
  output [3:0] MemControl,
  output [3:0] IOControl,
  output P0,
  output P1,
  output P2,
  output P3,
  output P4,
  output P5,
  output P6,
  output P7
);

  wire [3:3] and_1_out;

  and and_1 (and_1_out[3], Address[7], Address[6], Address[5], Address[4], Address[3]);
  Decoder #(.select(3)) decoder_1 (
    .out0(P0), .out1(P1), .out2(P2), .out3(P3), .out4(P4), .out5(P5), .out6(P6), .out7(P7),
    .sel(Address[2:0]), .en(and_1_out[3]));
  assign MemControl = Control & ~{4{and_1_out[3]}};  // AND_Gate and_2, 4 bits wide
  assign IOControl = Control & {4{and_1_out[3]}};  // AND_Gate and_3, 4 bits wide
endmodule
