// Logisim project ProtoOne.v1.2.circ as structural Verilog: 10 circuits, main circuit main
module main (
);

  wire ACCload, ADDRsel, button_1_out, Clk, clock_1_out, d_ff_1_q, FLAGSload, Halt, IRload, MARload, MDRload,
       PCinc, PCload, por_1_out;
  wire [2:0] ULAoper;
  wire [3:0] CtrlBus, memio_1_memcontrol;
  wire [7:0] acc_1_accout, flags_1_flagsout, ir_1_irout, mar_1_marout, mdr_1_dataout, mdr_1_dbusout,
       multiplexer_1_out, pc_1_pcout, ula_1_flags, ula_1_ulaout;

  Clock clock_1 (.out(clock_1_out));
  Button button_1 (.out(button_1_out));
  PC pc_1 (.PCload(PCload), .PCinc(PCinc), .CLKin(Clk), .Reset(CtrlBus[3]), .PCin(mdr_1_dataout), .PCout(pc_1_pcout));
  MAR mar_1 (.MARIn(mdr_1_dataout), .MARload(MARload), .ClkIn(Clk), .Reset(CtrlBus[3]), .MAROut(mar_1_marout));
  ACC acc_1 (.ACCload(ACCload), .AccIn(ula_1_ulaout), .ClkIn(Clk), .Reset(CtrlBus[3]), .AccOut(acc_1_accout));
  POR por_1 (.out(por_1_out));
  D_Flip_Flop d_ff_1 (.D(1'b1), .clk(clock_1_out), .Q(d_ff_1_q), .reset(CtrlBus[3]));  // open: Qn, preset
  or or_1 (CtrlBus[3], por_1_out, button_1_out);
  Multiplexer #(.width(8)) multiplexer_1 (.in0(pc_1_pcout), .in1(mar_1_marout), .out(multiplexer_1_out), .sel(ADDRsel));
  ULA ula_1 (.Y(mdr_1_dataout), .ULAoper(ULAoper), .X(acc_1_accout), .Flags(ula_1_flags), .ULAout(ula_1_ulaout));
  and and_1 (Clk, clock_1_out, d_ff_1_q);
  IDecoder idecoder_1 (
    .Clk(Clk), .Instr(ir_1_irout), .Flags(flags_1_flagsout), .Reset(CtrlBus[3]), .PCinc(PCinc),
    .PCload(PCload), .ACCload(ACCload), .MDRload(MDRload), .MARload(MARload), .IRload(IRload),
    .FLAGSload(FLAGSload), .MEMread(CtrlBus[1]), .MEMwrite(CtrlBus[0]), .ADDRsel(ADDRsel), .Halt(Halt),
    .ULAoper(ULAoper));
  MDR mdr_1 (
    .MDRload(MDRload), .Clk(Clk), .Rst(CtrlBus[3]), .MEMwrite(CtrlBus[0]), .MEMread(CtrlBus[1]),
    .DataIn(acc_1_accout), .DBusIn(mdr_1_dbusout), .DataOut(mdr_1_dataout), .DBusOut(mdr_1_dbusout));
  IR ir_1 (.IRIn(mdr_1_dbusout), .IRload(IRload), .ClkIn(Clk), .Reset(CtrlBus[3]), .IROut(ir_1_irout));
  Flags flags_1 (
    .FLAGSload(FLAGSload), .Clk(Clk), .Reset(CtrlBus[3]), .FlagsIn(ula_1_flags), .FlagsOut(flags_1_flagsout));
  MemIO memio_1 (
    .Control({CtrlBus[3], Clk, CtrlBus[1:0]}), .Address(multiplexer_1_out), .MemControl(memio_1_memcontrol));  // open: IOControl, P0, P1, P2, P3, P4, P5, P6, P7
  RAM #(.asyncread("true"), .databus("bidir"), .\type ("nonvolatile")) Memoria (
    .addr(multiplexer_1_out), .we(memio_1_memcontrol[0]), .oe(memio_1_memcontrol[1]),
    .clk(memio_1_memcontrol[2]), .data(mdr_1_dbusout));

  // Other names for the same wires on the sheet: MEMwrite = CtrlBus[0]; MEMread = CtrlBus[1]; CtrlBus[2] = Clk;
  //   Rst = CtrlBus[3]

  // Notes on the sheet:
  //   Barramento
  //   Dados
  //   Endereços
  //   Controle
endmodule

module ULA (
  input  [7:0] X,
  input  [7:0] Y,
  input  [2:0] ULAoper,
  output [7:0] Flags,
  output [7:0] ULAout
);

  wire [7:0] adder_1_out, and_1_out, not_1_out, or_1_out;

  Adder adder_1 (.a(Y), .b(X), .out(adder_1_out), .cin(1'b0), .cout(Flags[2]));
  assign and_1_out = Y & X;  // AND_Gate and_1, 8 bits wide
  assign or_1_out = Y | X;  // OR_Gate or_1, 8 bits wide
  assign not_1_out = ~X;  // NOT_Gate not_1, 8 bits wide
  Multiplexer #(.select(3), .width(8)) multiplexer_1 (
    .in0(adder_1_out), .in1(and_1_out), .in2(or_1_out), .in3(not_1_out), .in4(Y),
    .out({Flags[1], ULAout[6:0]}), .sel(ULAoper));  // open: in5, in6, in7
  nor nor_1 (Flags[0], ULAout[0], ULAout[1], ULAout[2], ULAout[3], ULAout[4], ULAout[5], ULAout[6], Flags[1]);

  assign ULAout[7] = Flags[1];
endmodule

module IDecoder (
  input  Reset,
  input  Clk,
  input  [7:0] Instr,
  input  [7:0] Flags,
  output PCinc,
  output PCload,
  output ACCload,
  output MDRload,
  output MARload,
  output IRload,
  output FLAGSload,
  output MEMread,
  output MEMwrite,
  output ADDRsel,
  output Halt,
  output [2:0] ULAoper
);

  wire and_1_out;
  wire [2:0] counter_1_q;

  Counter #(.max('h7), .width(3)) counter_1 (
    .clr(Reset), .load(1'b0), .up(1'b1), .count(1'b1), .clk(and_1_out), .Q(counter_1_q));  // open: D, carry
  and and_1 (and_1_out, ~Clk, ~Halt);  // AND_Gate
  ROM #(.addrWidth(9), .dataWidth(14)) rom_1 (
    .addr({Flags[0], Flags[1], Instr[7:4], counter_1_q}),
    .data({ULAoper, Halt, ADDRsel, MEMwrite, MEMread, FLAGSload, IRload, MARload, MDRload, ACCload, PCload, PCinc}));

  // Other names for the same wires on the sheet: Nin = Flags[1]; Zin = Flags[0]

  // Notes on the sheet:
  //   contents of rom_1 (hex, n*v repeats v):
  //   a0 1 6*0 a0 1 88 11 208 300 0 0 a0 1 88 11 288 2000 4 0 a0 1 88 11 288 0 44 0 a0 1 88 11 288 800 44
  //   0 a0 1 88 11 288 1000 44 0 a0 1 1800 44 4*0 e5 3a18 32ca 1059 126e 2bb5 1c53 16be a0 1 88 2 4*0 a0 1
  //   88 1 4*0 a0 1 88 1 4*0 2d4a 151a 31ab 22b5 2429 2fee 1de3 34ac 2887 ef5 932 e2e 1f91 12c9 bd7 31fc
  //   180d 11fb 28ed 18c6 3d03 c9d 3900 743 3f96 1f7e 3c93 7a7 1ef1 1d24 1b4a 275f a0 400 6*0 a0 1 6*0 a0
  //   1 88 11 208 300 0 0 a0 1 88 11 288 2000 4 0 a0 1 88 11 288 0 44 0 a0 1 88 11 288 800 44 0 a0 1 88 11
  //   288 1000 44 0 a0 1 1800 44 4*0 5ab 3f9a 2add 1511 2ddd 2d 44b 2e81 a0 1 88 2 4*0 a0 1 88 1 2 0 0 0
  //   a0 1 88 1 4*0 66f 1141 2590 152b 1715 3512 20e8 3445 3eac 1f59 1225 1c3b 1876 37d3 36e4 10b3 6f8
  //   25dc 1d6 e87 e2c 2675 353 1f09 2529 30b9 170 d5a 1059 31c6 1eaa cf0 a0 400 6*0 a0 1 6*0 a0 1 88 11
  //   208 300 0 0 a0 1 88 11 288 2000 4 0 a0 1 88 11 288 0 44 0 a0 1 88 11 288 800 44 0 a0 1 88 11 288
  //   1000 44 0 a0 1 1800 44 4*0 2d9a 7e3 2ac6 83 cb4 1b7 2d80 2dc3 a0 1 88 2 4*0 a0 1 88 1 4*0 a0 1 88 1
  //   2 0 0 0 37c8 2b4d 391a 2287 fc4 2b1a 2407 ee4 32bb 1c6b 3828 54c 1375 608 37df 2e4e 3de1 3f8 33de
  //   1212 3fa7 2699 3d08 19da 256b 7d3 3268 3349 1819 1288 34ad 22c6 a0 400 6*0 a0 1 6*0 a0 1 88 11 208
  //   300 0 0 a0 1 88 11 288 2000 4 0 a0 1 88 11 288 0 44 0 a0 1 88 11 288 800 44 0 a0 1 88 11 288 1000 44
  //   0 a0 1 1800 44 4*0 184e 2496 71e 2a05 178d 1a21 f3a 3a60 a0 1 88 2 4*0 a0 1 88 1 2 0 0 0 a0 1 88 1 2
  //   0 0 0 2bfd 1769 b37 264d 5af 1dec 192c 20a6 346 374e c81 46a 2b20 3768 3763 1632 2ce8 2af1 3c8e 15b8
  //   1f4b 62b 35d0 3ea5 cb3 a70 82d 2bd4 2473 21b4 2980 38a2 a0 400 15a9 a7f d82 12fb 175c 1ea3
endmodule

module PC (
  input  [7:0] PCin,
  input  PCload,
  input  PCinc,
  input  CLKin,
  input  Reset,
  output [7:0] PCout
);

  wire or_1_out;
  wire [7:0] adder_1_out, multiplexer_1_out;

  or or_1 (or_1_out, PCload, PCinc);
  Multiplexer #(.width(8)) multiplexer_1 (.in0(PCin), .in1(adder_1_out), .out(multiplexer_1_out), .sel(PCinc));
  Register register_1 (.D(multiplexer_1_out), .en(or_1_out), .clk(CLKin), .Q(PCout), .clr(Reset));
  Adder adder_1 (.a(PCout), .b(8'h1), .out(adder_1_out), .cin(1'b0));  // open: cout
endmodule

module MDR (
  input  [7:0] DataIn,
  input  [7:0] DBusIn,
  input  MEMread,
  input  MDRload,
  input  Clk,
  input  Rst,
  input  MEMwrite,
  output [7:0] DBusOut,
  output [7:0] DataOut
);

  wire [7:0] multiplexer_1_out;

  Register register_1 (.D(multiplexer_1_out), .en(MDRload), .clk(Clk), .Q(DataOut), .clr(Rst));
  Multiplexer #(.width(8)) multiplexer_1 (.in0(DataIn), .in1(DBusIn), .out(multiplexer_1_out), .sel(MEMread));
  assign DBusOut = MEMwrite ? DataOut : 8'bz;  // Controlled_Buffer controlled_buffer_1
endmodule

module MAR (
  input  [7:0] MARIn,
  input  MARload,
  input  ClkIn,
  input  Reset,
  output [7:0] MAROut
);

  Register register_1 (.D(MARIn), .en(MARload), .clk(ClkIn), .Q(MAROut), .clr(Reset));
endmodule

module ACC (
  input  [7:0] AccIn,
  input  ACCload,
  input  ClkIn,
  input  Reset,
  output [7:0] AccOut
);

  Register AC (.D(AccIn), .en(ACCload), .clk(ClkIn), .Q(AccOut), .clr(Reset));
endmodule

module IR (
  input  [7:0] IRIn,
  input  IRload,
  input  ClkIn,
  input  Reset,
  output [7:0] IROut
);

  Register register_1 (.D(IRIn), .en(IRload), .clk(ClkIn), .Q(IROut), .clr(Reset));
endmodule

module Flags (
  input  [7:0] FlagsIn,
  input  FLAGSload,
  input  Clk,
  input  Reset,
  output [7:0] FlagsOut
);

  Register Flags (.D(FlagsIn), .en(FLAGSload), .clk(Clk), .Q(FlagsOut), .clr(Reset));
  LED C (.in(FlagsOut[2]));
  LED N (.in(FlagsOut[1]));
  LED Z (.in(FlagsOut[0]));
endmodule

module MemIO (
  input  [3:0] Control,
  input  [7:0] Address,
  output [3:0] MemControl,
  output [3:0] IOControl,
  output P0,
  output P1,
  output P2,
  output P3,
  output P4,
  output P5,
  output P6,
  output P7
);

  wire [3:3] and_1_out;

  and and_1 (and_1_out[3], Address[7], Address[6], Address[5], Address[4], Address[3]);
  Decoder #(.select(3)) decoder_1 (
    .out0(P0), .out1(P1), .out2(P2), .out3(P3), .out4(P4), .out5(P5), .out6(P6), .out7(P7),
    .sel(Address[2:0]), .en(and_1_out[3]));
  assign MemControl = Control & ~{4{and_1_out[3]}};  // AND_Gate and_2, 4 bits wide
  assign IOControl = Control & {4{and_1_out[3]}};  // AND_Gate and_3, 4 bits wide
endmodule
