// Logisim project ProtoTwo v2.3.circ as structural Verilog: 6 circuits, main circuit SystemInside
module IDecoder (
  input  Clk,
  input  Reset,
  input  [7:0] Instr,
  input  [7:0] Flags,
  output PCinc,
  output PCload,
  output MDRload,
  output MARload,
  output IRload,
  output FLAGSload,
  output MEMread,
  output MEMwrite,
  output REGsrc,
  output REGload,
  output SPinc,
  output SPdec,
  output SPload,
  output ACCload,
  output [1:0] ADDRsel,
  output [1:0] DATAsel,
  output [3:0] ULAoper,
  output [2:0] REGsel
);

  wire and_1_out, cExec, Exec, Halt, multiplexer_1_out;
  wire [1:0] Conditions, JUMPsel, uJUMP;
  wire [5:0] adder_1_out, multiplexer_2_out, uAddress, uPC_q;
  wire [30:0] uProgram_data;

  PLA #(.in_width(8), .out_width(6), .\table ("00000xxx 000010 # AND\n00001xxx 000011 # OR\n00010xxx 000100 # XOR\n00011xxx 000101 # NOT\n00100xxx 000110 # ADD\n00101xxx 000111 # SUB\n00110xxx 001000 # DEC\n00111xxx 001001 # INC\n01000xxx 001010 # RR\n01001xxx 001011 # RL\n01010xxx 001100 # SRL\n01011xxx 001101 # SLL\n01100xxx 001110 # SRA\n01101xxx 001111 # MOV r\n10000xxx 010000 # MOV a\n10001xxx 010001 # LDD\n10010xxx 010101 # STD\n10011xxx 011001 # LDI\n10100xxx 011011 # PUSH\n10101xxx 011101 # POP\n10111xxx 011111 # MTSP\n11000xxx 100001 # CMP\n11110000 100010 # BZ\n11110001 010110 # BN\n11111000 101010 # CALL\n11111001 101110 # RET\n11111010 110000 # JMP\n11111111 110010 # HALT")) OpcodeTranslator (
    .in(Instr), .out(uAddress));
  Demultiplexer #(.width(2)) demultiplexer_1 (.out0(JUMPsel), .out1(Conditions), .in(uJUMP), .sel(cExec));
  Multiplexer #(.select(2)) multiplexer_1 (
    .in0(Flags[0]), .in1(Flags[1]), .in2(Flags[2]), .in3(Flags[3]), .out(multiplexer_1_out), .sel(Conditions));
  Multiplexer #(.select(2), .width(6)) multiplexer_2 (
    .in0({6{1'b0}}), .in1(uPC_q), .in2(adder_1_out), .in3(uAddress), .out(multiplexer_2_out), .sel(JUMPsel));
  and and_1 (and_1_out, ~Clk, ~Halt);  // AND_Gate
  or or_1 (Exec, ~cExec, multiplexer_1_out);  // OR_Gate
  Register #(.width(6)) uPC (.D(multiplexer_2_out), .en(1'b1), .clk(and_1_out), .Q(uPC_q), .clr(Reset));
  Adder #(.width(6)) adder_1 (.a(uPC_q), .b(6'b000001), .out(adder_1_out));  // open: cin, cout
  ROM #(.addrWidth(6), .dataWidth(31)) uProgram (
    .addr(uPC_q), .data({uProgram_data[30:22], cExec, uJUMP, uProgram_data[18:0]}));
  Multiplexer #(.enable("true"), .width(4)) multiplexer_3 (
    .in0(Instr[6:3]), .in1(uProgram_data[25:22]), .out(ULAoper), .sel(uProgram_data[26]), .en(Exec));
  Multiplexer #(.enable("true"), .width(3)) multiplexer_4 (
    .in0(Instr[2:0]), .in1(uProgram_data[29:27]), .out(REGsel), .sel(uProgram_data[30]), .en(Exec));
  assign PCinc = Exec ? uProgram_data[0] : 1'bz;  // Controlled_Buffer controlled_buffer_1
  assign PCload = Exec ? uProgram_data[1] : 1'bz;  // Controlled_Buffer controlled_buffer_2
  assign MDRload = Exec ? uProgram_data[2] : 1'bz;  // Controlled_Buffer controlled_buffer_3
  assign MARload = Exec ? uProgram_data[3] : 1'bz;  // Controlled_Buffer controlled_buffer_4
  assign IRload = Exec ? uProgram_data[4] : 1'bz;  // Controlled_Buffer controlled_buffer_5
  assign FLAGSload = Exec ? uProgram_data[5] : 1'bz;  // Controlled_Buffer controlled_buffer_6
  assign MEMread = Exec ? uProgram_data[6] : 1'bz;  // Controlled_Buffer controlled_buffer_7
  assign MEMwrite = Exec ? uProgram_data[7] : 1'bz;  // Controlled_Buffer controlled_buffer_8
  assign REGsrc = Exec ? uProgram_data[8] : 1'bz;  // Controlled_Buffer controlled_buffer_9
  assign REGload = Exec ? uProgram_data[9] : 1'bz;  // Controlled_Buffer controlled_buffer_10
  assign SPinc = Exec ? uProgram_data[10] : 1'bz;  // Controlled_Buffer controlled_buffer_11
  assign SPdec = Exec ? uProgram_data[11] : 1'bz;  // Controlled_Buffer controlled_buffer_12
  assign SPload = Exec ? uProgram_data[12] : 1'bz;  // Controlled_Buffer controlled_buffer_13
  assign Halt = Exec ? uProgram_data[13] : 1'bz;  // Controlled_Buffer controlled_buffer_14
  assign ACCload = Exec ? uProgram_data[14] : 1'bz;  // Controlled_Buffer controlled_buffer_15
  assign ADDRsel = Exec ? uProgram_data[16:15] : 2'bz;  // Controlled_Buffer controlled_buffer_16
  assign DATAsel = Exec ? uProgram_data[18:17] : 2'bz;  // Controlled_Buffer controlled_buffer_17
  Pull_Resistor pull_resistor_1 (.node(PCinc));
  Pull_Resistor pull_resistor_2 (.node(PCload));
  Pull_Resistor pull_resistor_3 (.node(MDRload));
  Pull_Resistor pull_resistor_4 (.node(MARload));
  Pull_Resistor pull_resistor_5 (.node(IRload));
  Pull_Resistor pull_resistor_6 (.node(FLAGSload));
  Pull_Resistor pull_resistor_7 (.node(MEMread));
  Pull_Resistor pull_resistor_8 (.node(MEMwrite));
  Pull_Resistor pull_resistor_9 (.node(REGsrc));
  Pull_Resistor pull_resistor_10 (.node(REGload));
  Pull_Resistor pull_resistor_11 (.node(SPinc));
  Pull_Resistor pull_resistor_12 (.node(SPdec));
  Pull_Resistor pull_resistor_13 (.node(SPload));
  Pull_Resistor pull_resistor_14 (.node(Halt));
  Pull_Resistor pull_resistor_15 (.node(ACCload));
  Pull_Resistor pull_resistor_16 (.node(ADDRsel));
  Pull_Resistor pull_resistor_17 (.node(DATAsel));

  // Other names for the same wires on the sheet: uJUMP[2] = cExec; Zin = Flags[0]; Nin = Flags[1]; Cin = Flags[2];
  //   Vin = Flags[3]; REGx[2:0] = Instr[2:0]; OPERx[3:0] = Instr[6:3]

  // Notes on the sheet:
  //   Execução condicional de uInstruções
  //   Conditions Zin Nin Cin Vin Exec
  //          00   0   x   x   x   0
  //          00   1   x   x   x   1
  //          01   x   0   x   x   0
  //          01   x   1   x   x   1
  //          10   x   x   0   x   0
  //          10   x   x   1   x   1
  //          11   x   x   x   0   0
  //          11   x   x   x   1   1
  //   contents of uProgram (hex, n*v repeats v):
  //   108050 180001 13*4020 300 4000 108044 100009 110044 200 108044 100009 160004 10080 108044 201 160804
  //   18080 118044 200 160004 1000 108044 100001 200002 0 108044 100001 280002 0 120804 118081 108044 2
  //   118044 2 108044 2 2000
endmodule

module CPU (
  input  [7:0] Dout,
  input  MasterClk,
  input  MasterRst,
  output [7:0] Address,
  output [3:0] Control,
  output [7:0] Din
);

  wire ACCload, d_ff_1_q, FLAGSload, IRload, MARload, MDRload, PCinc, PCload, por_1_out, REGload, REGsrc,
       SPdec, SPinc, SPload;
  wire [1:0] ADDRsel, DATAsel;
  wire [2:0] REGsel;
  wire [3:0] ULAoper;
  wire [7:0] flags_1_flagsout, ir_1_irout, mar_1_marout, mdr_1_dataout, multiplexer_1_out, multiplexer_3_out,
       pc_1_pcout, registerfile_1_a, registerfile_1_b, sp_1_spout, ula_1_flags, ula_1_ulaout;

  Multiplexer #(.width(8)) multiplexer_1 (
    .in0(mdr_1_dataout), .in1(ula_1_ulaout), .out(multiplexer_1_out), .sel(REGsrc));
  PC pc_1 (
    .PCload(PCload), .PCinc(PCinc), .CLKin(Control[2]), .Reset(Control[3]), .PCin(mdr_1_dataout),
    .PCout(pc_1_pcout));
  MAR mar_1 (.MARIn(mdr_1_dataout), .MARload(MARload), .ClkIn(Control[2]), .Reset(Control[3]), .MAROut(mar_1_marout));
  SP sp_1 (
    .SPload(SPload), .SPinc(SPinc), .SPdec(SPdec), .CLKin(Control[2]), .Reset(Control[3]),
    .SPin(mdr_1_dataout), .SPout(sp_1_spout));
  RegisterFile registerfile_1 (
    .ACCload(ACCload), .REGload(REGload), .Clk(Control[2]), .Rst(Control[3]), .REGsel(REGsel),
    .REGin(multiplexer_1_out), .ACCin(ula_1_ulaout), .B(registerfile_1_b), .A(registerfile_1_a));
  POR por_1 (.out(por_1_out));
  D_Flip_Flop d_ff_1 (.D(1'b1), .clk(MasterClk), .Q(d_ff_1_q), .reset(Control[3]));  // open: Qn, preset
  or or_1 (Control[3], por_1_out, MasterRst);
  Multiplexer #(.select(2), .width(8)) multiplexer_2 (
    .in1(pc_1_pcout), .in2(mar_1_marout), .in3(sp_1_spout), .out(Address), .sel(ADDRsel));  // open: in0
  Multiplexer #(.select(2), .width(8)) multiplexer_3 (
    .in0(registerfile_1_a), .in1(pc_1_pcout), .in2(sp_1_spout), .in3(registerfile_1_b),
    .out(multiplexer_3_out), .sel(DATAsel));
  ULA ula_1 (.ULAoper(ULAoper), .X(registerfile_1_a), .Y(registerfile_1_b), .Flags(ula_1_flags), .ULAout(ula_1_ulaout));
  and and_1 (Control[2], MasterClk, d_ff_1_q);
  MDR mdr_1 (
    .MDRload(MDRload), .Clk(Control[2]), .Rst(Control[3]), .MEMwrite(Control[0]), .MEMread(Control[1]),
    .DataIn(multiplexer_3_out), .DBusIn(Dout), .DataOut(mdr_1_dataout), .DBusOut(Din));
  IR ir_1 (.ClkIn(Control[2]), .IRIn(Dout), .IRload(IRload), .Reset(Control[3]), .IROut(ir_1_irout));
  Flags flags_1 (
    .Clk(Control[2]), .Reset(Control[3]), .FlagsIn(ula_1_flags), .FLAGSload(FLAGSload),
    .FlagsOut(flags_1_flagsout));
  IDecoder idecoder_1 (
    .Clk(Control[2]), .Reset(Control[3]), .Instr(ir_1_irout), .Flags(flags_1_flagsout), .PCinc(PCinc),
    .PCload(PCload), .MDRload(MDRload), .MARload(MARload), .IRload(IRload), .FLAGSload(FLAGSload),
    .MEMread(Control[1]), .MEMwrite(Control[0]), .REGsrc(REGsrc), .REGload(REGload), .SPinc(SPinc),
    .SPdec(SPdec), .SPload(SPload), .ACCload(ACCload), .ADDRsel(ADDRsel), .DATAsel(DATAsel),
    .ULAoper(ULAoper), .REGsel(REGsel));

  // Other names for the same wires on the sheet: CtrlBus[3:0] = Control; MEMwrite = Control[0]; MEMread = Control[1];
  //   Clk = Control[2]; Rst = Control[3]
endmodule

module SystemInside (
);

  wire ACCload, Clk, d_ff_1_q, FLAGSload, IRload, MARload, MasterClk_out, MasterRst_out, MDRload, PCinc,
       PCload, por_1_out, REGload, REGsrc, SPdec, SPinc, SPload;
  wire [1:0] ADDRsel, DATAsel;
  wire [2:0] REGsel;
  wire [3:0] CtrlBus, memio_1_memcontrol, ULAoper;
  wire [7:0] flags_1_flagsout, ir_1_irout, mar_1_marout, mdr_1_dataout, mdr_1_dbusout, multiplexer_1_out,
       multiplexer_2_out, multiplexer_3_out, pc_1_pcout, registerfile_1_a, registerfile_1_b, sp_1_spout,
       ula_1_flags, ula_1_ulaout;

  Multiplexer #(.width(8)) multiplexer_1 (
    .in0(mdr_1_dataout), .in1(ula_1_ulaout), .out(multiplexer_1_out), .sel(REGsrc));
  Clock MasterClk (.out(MasterClk_out));
  Button MasterRst (.out(MasterRst_out));
  PC pc_1 (.PCload(PCload), .PCinc(PCinc), .CLKin(Clk), .Reset(CtrlBus[3]), .PCin(mdr_1_dataout), .PCout(pc_1_pcout));
  MAR mar_1 (.MARIn(mdr_1_dataout), .MARload(MARload), .ClkIn(Clk), .Reset(CtrlBus[3]), .MAROut(mar_1_marout));
  SP sp_1 (
    .SPload(SPload), .SPinc(SPinc), .SPdec(SPdec), .CLKin(Clk), .Reset(CtrlBus[3]), .SPin(mdr_1_dataout),
    .SPout(sp_1_spout));
  RegisterFile registerfile_1 (
    .ACCload(ACCload), .REGload(REGload), .Clk(Clk), .Rst(CtrlBus[3]), .REGsel(REGsel),
    .REGin(multiplexer_1_out), .ACCin(ula_1_ulaout), .B(registerfile_1_b), .A(registerfile_1_a));
  POR por_1 (.out(por_1_out));
  ULA ula_1 (.ULAoper(ULAoper), .X(registerfile_1_a), .Y(registerfile_1_b), .Flags(ula_1_flags), .ULAout(ula_1_ulaout));
  D_Flip_Flop d_ff_1 (.D(1'b1), .clk(MasterClk_out), .Q(d_ff_1_q), .reset(CtrlBus[3]));  // open: Qn, preset
  or or_1 (CtrlBus[3], por_1_out, MasterRst_out);
  Multiplexer #(.select(2), .width(8)) multiplexer_2 (
    .in1(pc_1_pcout), .in2(mar_1_marout), .in3(sp_1_spout), .out(multiplexer_2_out), .sel(ADDRsel));  // open: in0
  Multiplexer #(.select(2), .width(8)) multiplexer_3 (
    .in0(registerfile_1_a), .in1(pc_1_pcout), .in2(sp_1_spout), .in3(registerfile_1_b),
    .out(multiplexer_3_out), .sel(DATAsel));
  and and_1 (Clk, MasterClk_out, d_ff_1_q);
  MDR mdr_1 (
    .MDRload(MDRload), .Clk(Clk), .Rst(CtrlBus[3]), .MEMwrite(CtrlBus[0]), .MEMread(CtrlBus[1]),
    .DataIn(multiplexer_3_out), .DBusIn(mdr_1_dbusout), .DataOut(mdr_1_dataout), .DBusOut(mdr_1_dbusout));
  IR ir_1 (.ClkIn(Clk), .IRIn(mdr_1_dbusout), .IRload(IRload), .Reset(CtrlBus[3]), .IROut(ir_1_irout));
  Flags flags_1 (
    .Clk(Clk), .Reset(CtrlBus[3]), .FlagsIn(ula_1_flags), .FLAGSload(FLAGSload), .FlagsOut(flags_1_flagsout));
  IDecoder idecoder_1 (
    .Clk(Clk), .Reset(CtrlBus[3]), .Instr(ir_1_irout), .Flags(flags_1_flagsout), .PCinc(PCinc),
    .PCload(PCload), .MDRload(MDRload), .MARload(MARload), .IRload(IRload), .FLAGSload(FLAGSload),
    .MEMread(CtrlBus[1]), .MEMwrite(CtrlBus[0]), .REGsrc(REGsrc), .REGload(REGload), .SPinc(SPinc),
    .SPdec(SPdec), .SPload(SPload), .ACCload(ACCload), .ADDRsel(ADDRsel), .DATAsel(DATAsel),
    .ULAoper(ULAoper), .REGsel(REGsel));
  MemIO memio_1 (
    .Control({CtrlBus[3], Clk, CtrlBus[1:0]}), .Address(multiplexer_2_out), .MemControl(memio_1_memcontrol));  // open: IOControl, P0, P1, P2, P3, P4, P5, P6, P7
  RAM #(.asyncread("true"), .databus("bidir"), .\type ("nonvolatile")) Memoria (
    .addr(multiplexer_2_out), .we(memio_1_memcontrol[0]), .oe(memio_1_memcontrol[1]),
    .clk(memio_1_memcontrol[2]), .data(mdr_1_dbusout));

  // Other names for the same wires on the sheet: MEMwrite = CtrlBus[0]; MEMread = CtrlBus[1]; CtrlBus[2] = Clk;
  //   Rst = CtrlBus[3]

  // Notes on the sheet:
  //   Barramento
  //   Dados
  //   Endereços
  //   Controle
endmodule

module SystemBlocks (
);

  wire button_1_out, clock_1_out, keyboard_1_avail, keyboardcontroller_1_clk, memio_1_p0,
       ttycontroller_1_clear, ttycontroller_1_clk, ttycontroller_1_we, undriven, undriven_2;
  wire [3:0] cpu_1_control, memio_1_iocontrol, memio_1_memcontrol;
  wire [6:0] keyboard_1_data, ttycontroller_1_data;
  wire [7:0] cpu_1_address, cpu_1_din;

  Clock clock_1 (.out(clock_1_out));
  CPU cpu_1 (
    .MasterClk(clock_1_out), .MasterRst(button_1_out), .Dout(cpu_1_din), .Address(cpu_1_address),
    .Control(cpu_1_control), .Din(cpu_1_din));
  Button button_1 (.out(button_1_out));
  MemIO memio_1 (
    .Control(cpu_1_control), .Address(cpu_1_address), .IOControl(memio_1_iocontrol), .P0(memio_1_p0),
    .MemControl(memio_1_memcontrol));  // open: P1, P2, P3, P4, P5, P6, P7
  RAM #(.asyncread("true"), .databus("bidir"), .\type ("nonvolatile")) Memoria (
    .addr(cpu_1_address), .we(memio_1_memcontrol[0]), .oe(memio_1_memcontrol[1]),
    .clk(memio_1_memcontrol[2]), .data(cpu_1_din));
  // Probe on memio_1_iocontrol
  TTY tty_1 (
    .data(ttycontroller_1_data), .clk(ttycontroller_1_clk), .we(ttycontroller_1_we),
    .clr(ttycontroller_1_clear));
  TTYcontroller ttycontroller_1 (
    .EN(memio_1_p0), .IO(memio_1_iocontrol), .Din(cpu_1_din), .Data(ttycontroller_1_data),
    .Clear(ttycontroller_1_clear), .WE(ttycontroller_1_we), .Clk(ttycontroller_1_clk));
  Keyboard keyboard_1 (
    .clk(keyboardcontroller_1_clk), .re(undriven), .clr(undriven_2), .avail(keyboard_1_avail),
    .data(keyboard_1_data));
  KeyboardController keyboardcontroller_1 (
    .RE(undriven), .Clear(undriven_2), .IO(memio_1_iocontrol), .Aval(keyboard_1_avail),
    .Clk(keyboardcontroller_1_clk), .Data(keyboard_1_data));

  // Notes on the sheet:
  //   Barramento
  //   Dados
  //   Endereços
  //   Controle
endmodule

module TTYcontroller (
  input  [3:0] IO,
  input  EN,
  input  [7:0] Din,
  output WE,
  output Clk,
  output Clear,
  output [6:0] Data
);

  wire and_2_out;

  and and_1 (WE, IO[0], EN);
  or or_1 (Clear, IO[3], and_2_out);
  and and_2 (and_2_out, EN, Din[7]);

  assign Clk = IO[2];
  assign Data = Din[6:0];
endmodule

module KeyboardController (
  input  [3:0] IO,
  input  Aval,
  input  RE,
  input  Clear,
  output Clk,
  output [6:0] Data
);
endmodule
