// Logisim project ProtoTwo_Base.circ as structural Verilog: 9 circuits, main circuit ULA
module ULA (
  input  [3:0] ULAoper,
  input  [7:0] X,
  input  [7:0] Y,
  output [7:0] Flags,
  output [7:0] ULAout
);

  wire adder_1_cout, and_3_out, CS, multiplexer_3_out, multiplexer_4_out, or_2_out, P, VS;
  wire [6:0] adder_1_out;
  wire [7:0] and_1_out, and_2_out, multiplexer_1_out, not_1_out, or_1_out, shifter_1_out, shifter_2_out,
       shifter_3_out, shifter_4_out, shifter_5_out, xor_1_out, xor_2_out;
  wire [7:7] adder_2_out, enB, invB;

  Multiplexer #(.width(8)) multiplexer_1 (.in0(Y), .in1(X), .out(multiplexer_1_out), .sel(enB[7]));
  assign and_1_out = {8{enB[7]}} & Y;  // AND_Gate and_1, 8 bits wide
  assign xor_1_out = {8{invB[7]}} ^ and_1_out;  // XOR_Gate xor_1, 8 bits wide
  assign and_2_out = X & Y;  // AND_Gate and_2, 8 bits wide
  assign or_1_out = X | Y;  // OR_Gate or_1, 8 bits wide
  assign xor_2_out = X ^ Y;  // XOR_Gate xor_2, 8 bits wide
  assign not_1_out = ~Y;  // NOT_Gate not_1, 8 bits wide
  Adder #(.width(7)) adder_1 (
    .a(multiplexer_1_out[6:0]), .b(xor_1_out[6:0]), .out(adder_1_out), .cin(ULAoper[0]), .cout(adder_1_cout));
  Adder #(.width(1)) adder_2 (
    .a(multiplexer_1_out[7]), .b(xor_1_out[7]), .out(adder_2_out[7]), .cin(adder_1_cout), .cout(CS));
  Shifter #(.shift("rr")) shifter_1 (.in(Y), .\dist (3'b001), .out(shifter_1_out));
  Shifter #(.shift("rl")) shifter_2 (.in(Y), .\dist (3'b001), .out(shifter_2_out));
  Shifter #(.shift("lr")) shifter_3 (.in(Y), .\dist (3'b001), .out(shifter_3_out));
  Shifter shifter_4 (.in(Y), .\dist (3'b001), .out(shifter_4_out));
  Shifter #(.shift("ar")) shifter_5 (.in(Y), .\dist (3'b001), .out(shifter_5_out));
  xor xor_3 (VS, adder_1_cout, CS);
  Multiplexer #(.select(4), .width(8)) multiplexer_2 (
    .in0(and_2_out), .in1(or_1_out), .in2(xor_2_out), .in3(not_1_out), .in4({adder_2_out[7], adder_1_out}),
    .in5({adder_2_out[7], adder_1_out}), .in6({adder_2_out[7], adder_1_out}),
    .in7({adder_2_out[7], adder_1_out}), .in8(shifter_1_out), .in9(shifter_2_out), .in10(shifter_3_out),
    .in11(shifter_4_out), .in12(shifter_5_out), .in13(Y), .out({Flags[1], ULAout[6:0]}), .sel(ULAoper));  // open: in14, in15
  Multiplexer multiplexer_3 (.in0(1'b0), .in1(CS), .out(multiplexer_3_out), .sel(ULAoper[2]));
  Multiplexer multiplexer_4 (.in0(Y[0]), .in1(Y[7]), .out(multiplexer_4_out), .sel(ULAoper[0]));
  not not_2 (enB[7], ULAoper[1]);
  nor nor_1 (Flags[0], ULAout[0], ULAout[1], ULAout[2], ULAout[3], ULAout[4], ULAout[5], ULAout[6], Flags[1]);
  ExactlyOne xor_4 (
    .out(P), .in0(ULAout[0]), .in1(ULAout[1]), .in2(ULAout[2]), .in3(ULAout[3]), .in4(ULAout[4]),
    .in5(ULAout[5]), .in6(ULAout[6]), .in7(Flags[1]));
  Multiplexer multiplexer_5 (.in0(multiplexer_3_out), .in1(multiplexer_4_out), .out(Flags[2]), .sel(or_2_out));
  or or_2 (or_2_out, ULAoper[3], ULAoper[2]);
  Multiplexer multiplexer_6 (.in0(P), .in1(VS), .out(Flags[3]), .sel(and_3_out));
  and and_3 (and_3_out, ~ULAoper[3], ULAoper[2]);  // AND_Gate
  xor xor_5 (invB[7], ULAoper[0], ULAoper[1]);

  assign ULAout[7] = Flags[1];

  // Other names for the same wires on the sheet: enB[6:0] = {7{enB[7]}}; selA = enB[7]; C = Flags[2]; V = Flags[3];
  //   invB[6:0] = {7{invB[7]}}; inc = ULAoper[0]; oper[3:0] = ULAoper; b0 = Y[0]; b7 = Y[7]

  // Notes on the sheet:
  //   ULAoper
  //   0000 X AND Y
  //   0001 X OR Y
  //   0010 X XOR Y
  //   0011 NOT Y
  //   0100 X + Y
  //   0101 X - Y
  //   0110 DEC Y
  //   0111 INC Y
  //   1000 RR Y
  //   1001 RL Y
  //   1010 SRL Y
  //   1011 SLL Y
  //   1100 SRA Y
  //   0000 Y
  //   0000 N.D.
  //   0000 N.D.
endmodule

module PC (
  input  [7:0] PCin,
  input  PCload,
  input  PCinc,
  input  CLKin,
  input  Reset,
  output [7:0] PCout
);

  wire or_1_out;
  wire [7:0] adder_1_out, multiplexer_1_out;

  or or_1 (or_1_out, PCload, PCinc);
  Multiplexer #(.width(8)) multiplexer_1 (.in0(PCin), .in1(adder_1_out), .out(multiplexer_1_out), .sel(PCinc));
  Register register_1 (.D(multiplexer_1_out), .en(or_1_out), .clk(CLKin), .Q(PCout), .clr(Reset));
  Adder adder_1 (.a(PCout), .b(8'h1), .out(adder_1_out), .cin(1'b0));  // open: cout
endmodule

module MDR (
  input  [7:0] DataIn,
  input  [7:0] DBusIn,
  input  MEMread,
  input  MDRload,
  input  Clk,
  input  Rst,
  input  MEMwrite,
  output [7:0] DBusOut,
  output [7:0] DataOut
);

  wire [7:0] multiplexer_1_out;

  Register register_1 (.D(multiplexer_1_out), .en(MDRload), .clk(Clk), .Q(DataOut), .clr(Rst));
  Multiplexer #(.width(8)) multiplexer_1 (.in0(DataIn), .in1(DBusIn), .out(multiplexer_1_out), .sel(MEMread));
  assign DBusOut = MEMwrite ? DataOut : 8'bz;  // Controlled_Buffer controlled_buffer_1
endmodule

module MAR (
  input  [7:0] MARIn,
  input  MARload,
  input  ClkIn,
  input  Reset,
  output [7:0] MAROut
);

  Register register_1 (.D(MARIn), .en(MARload), .clk(ClkIn), .Q(MAROut), .clr(Reset));
endmodule

module IR (
  input  [7:0] IRIn,
  input  IRload,
  input  ClkIn,
  input  Reset,
  output [7:0] IROut
);

  Register register_1 (.D(IRIn), .en(IRload), .clk(ClkIn), .Q(IROut), .clr(Reset));
endmodule

module SP (
  input  [7:0] SPin,
  input  SPload,
  input  SPinc,
  input  SPdec,
  input  CLKin,
  input  Reset,
  output [7:0] SPout
);

  wire or_1_out, or_2_out;
  wire [7:0] adder_1_out, multiplexer_1_out, multiplexer_2_out;

  or or_1 (or_1_out, SPinc, SPdec);
  or or_2 (or_2_out, SPload, or_1_out);
  Multiplexer #(.width(8)) multiplexer_1 (.in0(SPin), .in1(adder_1_out), .out(multiplexer_1_out), .sel(or_1_out));
  Register register_1 (.D(multiplexer_1_out), .en(or_2_out), .clk(CLKin), .Q(SPout), .clr(Reset));
  Multiplexer #(.width(8)) multiplexer_2 (.in0(8'h1), .in1({8{1'b1}}), .out(multiplexer_2_out), .sel(SPdec));
  Adder adder_1 (.a(SPout), .b(multiplexer_2_out), .out(adder_1_out), .cin(1'b0));  // open: cout
endmodule

module RegisterFile (
  input  [2:0] REGsel,
  input  [7:0] ACCin,
  input  [7:0] REGin,
  input  ACCload,
  input  REGload,
  input  Clk,
  input  Rst,
  output [7:0] A,
  output [7:0] B
);

  wire decoder_1_out0, decoder_1_out1, decoder_1_out2, decoder_1_out3, decoder_1_out4, decoder_1_out5,
       decoder_1_out6, decoder_1_out7, or_1_out;
  wire [7:0] multiplexer_1_out, R1_q, R2_q, R3_q, R4_q, R5_q, R6_q, R7_q;

  Decoder #(.select(3)) decoder_1 (
    .out0(decoder_1_out0), .out1(decoder_1_out1), .out2(decoder_1_out2), .out3(decoder_1_out3),
    .out4(decoder_1_out4), .out5(decoder_1_out5), .out6(decoder_1_out6), .out7(decoder_1_out7), .sel(REGsel),
    .en(REGload));
  Multiplexer #(.width(8)) multiplexer_1 (.in0(ACCin), .in1(REGin), .out(multiplexer_1_out), .sel(decoder_1_out0));
  Register R0 (.D(multiplexer_1_out), .en(or_1_out), .clk(Clk), .Q(A), .clr(Rst));
  or or_1 (or_1_out, ACCload, decoder_1_out0);
  Register R1 (.D(REGin), .en(decoder_1_out1), .clk(Clk), .Q(R1_q), .clr(Rst));
  Register R2 (.D(REGin), .en(decoder_1_out2), .clk(Clk), .Q(R2_q), .clr(Rst));
  Register R3 (.D(REGin), .en(decoder_1_out3), .clk(Clk), .Q(R3_q), .clr(Rst));
  Register R4 (.D(REGin), .en(decoder_1_out4), .clk(Clk), .Q(R4_q), .clr(Rst));
  Register R5 (.D(REGin), .en(decoder_1_out5), .clk(Clk), .Q(R5_q), .clr(Rst));
  Register R6 (.D(REGin), .en(decoder_1_out6), .clk(Clk), .Q(R6_q), .clr(Rst));
  Register R7 (.D(REGin), .en(decoder_1_out7), .clk(Clk), .Q(R7_q), .clr(Rst));
  Multiplexer #(.select(3), .width(8)) multiplexer_2 (
    .in0(A), .in1(R1_q), .in2(R2_q), .in3(R3_q), .in4(R4_q), .in5(R5_q), .in6(R6_q), .in7(R7_q), .out(B),
    .sel(REGsel));
endmodule

module Flags (
  input  [7:0] FlagsIn,
  input  FLAGSload,
  input  Clk,
  input  Reset,
  output [7:0] FlagsOut
);

  Register Flags (.D(FlagsIn), .en(FLAGSload), .clk(Clk), .Q(FlagsOut), .clr(Reset));
  LED V (.in(FlagsOut[3]));
  LED C (.in(FlagsOut[2]));
  LED N (.in(FlagsOut[1]));
  LED Z (.in(FlagsOut[0]));
endmodule

module MemIO (
  input  [3:0] Control,
  input  [7:0] Address,
  output [3:0] MemControl,
  output [3:0] IOControl,
  output P0,
  output P1,
  output P2,
  output P3,
  output P4,
  output P5,
  output P6,
  output P7
);

  wire [3:3] and_1_out;

  and and_1 (and_1_out[3], Address[7], Address[6], Address[5], Address[4], Address[3]);
  Decoder #(.select(3)) decoder_1 (
    .out0(P0), .out1(P1), .out2(P2), .out3(P3), .out4(P4), .out5(P5), .out6(P6), .out7(P7),
    .sel(Address[2:0]), .en(and_1_out[3]));
  assign MemControl = Control & ~{4{and_1_out[3]}};  // AND_Gate and_2, 4 bits wide
  assign IOControl = Control & {4{and_1_out[3]}};  // AND_Gate and_3, 4 bits wide
endmodule
