// Logisim project ProtoZero v2.3.circ as structural Verilog: 12 circuits, main circuit CPU
module CPU (
  input  Clock,
  input  Reset
);

  wire Clk, d_ff_1_q, DATAsel, FLAGSload, Halt, Hload, IRload, MARload, MDRload, PCinc, PCload, por_1_out,
       SPdec, SPinc, SPload;
  wire [1:0] ADDRsel;
  wire [2:0] ULAoper;
  wire [3:0] CtrlBus, memio_1_memcontrol;
  wire [7:0] flags_1_flagsout, h_1_accout, ir_1_irout, mar_1_marout, mdr_1_dataout, mdr_1_dbusout,
       multiplexer_1_out, multiplexer_2_out, pc_1_pcout, sp_1_spout, ula_1_flags, ula_1_ulaout;

  Multiplexer #(.width(8)) multiplexer_1 (
    .in0(ula_1_ulaout), .in1(mdr_1_dataout), .out(multiplexer_1_out), .sel(DATAsel));
  PC pc_1 (.PCout(pc_1_pcout), .PCload(PCload), .PCinc(PCinc), .CLKin(Clk), .Reset(CtrlBus[3]), .PCin(mdr_1_dataout));
  MAR mar_1 (.MAROut(mar_1_marout), .MARIn(mdr_1_dataout), .MARload(MARload), .ClkIn(Clk), .Reset(CtrlBus[3]));
  SP sp_1 (
    .SPout(sp_1_spout), .SPin(mdr_1_dataout), .CLKin(Clk), .Reset(CtrlBus[3]), .SPload(SPload),
    .Spdec(SPdec), .SPinc(SPinc));
  H h_1 (.AccOut(h_1_accout), .AccIn(multiplexer_1_out), .ACCload(Hload), .ClkIn(Clk), .Reset(CtrlBus[3]));
  POR por_1 (.out(por_1_out));
  D_Flip_Flop d_ff_1 (.D(1'b1), .clk(Clock), .Q(d_ff_1_q), .reset(CtrlBus[3]));  // open: Qn, preset
  or or_1 (CtrlBus[3], por_1_out, Reset);
  and and_1 (Clk, Clock, d_ff_1_q);
  Multiplexer #(.select(2), .width(8)) multiplexer_2 (
    .in1(pc_1_pcout), .in2(mar_1_marout), .in3(sp_1_spout), .out(multiplexer_2_out), .sel(ADDRsel));  // open: in0
  ULA ula_1 (.ULAout(ula_1_ulaout), .Flags(ula_1_flags), .ULAoper(ULAoper), .X(h_1_accout), .Y(mdr_1_dataout));
  IDecoder idecoder_1 (
    .PCinc(PCinc), .PCload(PCload), .Hload(Hload), .MDRload(MDRload), .MARload(MARload), .IRload(IRload),
    .SPinc(SPinc), .SPdec(SPdec), .SPload(SPload), .FLAGSload(FLAGSload), .MEMread(CtrlBus[1]),
    .MEMwrite(CtrlBus[0]), .ADDRsel(ADDRsel), .DATAsel(DATAsel), .Halt(Halt), .ULAoper(ULAoper), .Clk(Clk),
    .Reset(CtrlBus[3]), .Instr(ir_1_irout), .Flags(flags_1_flagsout));
  MDR mdr_1 (
    .DataOut(mdr_1_dataout), .DBusOut(mdr_1_dbusout), .MDRload(MDRload), .Clk(Clk), .Rst(CtrlBus[3]),
    .MEMwrite(CtrlBus[0]), .MEMread(CtrlBus[1]), .DataIn(h_1_accout), .DBusIn(mdr_1_dbusout));
  IR ir_1 (.IROut(ir_1_irout), .IRIn(mdr_1_dbusout), .IRload(IRload), .ClkIn(Clk), .Reset(CtrlBus[3]));
  Flags flags_1 (
    .FlagsOut(flags_1_flagsout), .FlagsIn(ula_1_flags), .FLAGSload(FLAGSload), .Clk(Clk), .Reset(CtrlBus[3]));
  MemIO memio_1 (
    .MemControl(memio_1_memcontrol), .Control({CtrlBus[3], Clk, CtrlBus[1:0]}), .Address(multiplexer_2_out));  // open: IOControl, P0, P1, P2, P3, P4, P5, P6, P7
  RAM #(.asyncread("true"), .databus("bidir"), .\type ("nonvolatile")) Memoria (
    .addr(multiplexer_2_out), .we(memio_1_memcontrol[0]), .oe(memio_1_memcontrol[1]),
    .clk(memio_1_memcontrol[2]), .data(mdr_1_dbusout));

  // Other names for the same wires on the sheet: MEMwrite = CtrlBus[0]; MEMread = CtrlBus[1]; CtrlBus[2] = Clk;
  //   Rst = CtrlBus[3]

  // Notes on the sheet:
  //   Barramento
  //   Controle
  //   Dados
  //   Endereços
endmodule

module ULA (
  input  [7:0] Y,
  input  [7:0] X,
  input  [2:0] ULAoper,
  output [7:0] Flags,
  output [7:0] ULAout
);

  wire [7:0] adder_1_out, and_1_out, negator_1_out, or_1_out, subtractor_1_out;

  Adder adder_1 (.a(Y), .b(X), .out(adder_1_out), .cin(1'b0), .cout(Flags[2]));
  assign and_1_out = Y & X;  // AND_Gate and_1, 8 bits wide
  assign or_1_out = Y | X;  // OR_Gate or_1, 8 bits wide
  Multiplexer #(.select(3), .width(8)) multiplexer_1 (
    .in0(adder_1_out), .in1(and_1_out), .in2(or_1_out), .in3(negator_1_out), .in4(subtractor_1_out),
    .out({Flags[1], ULAout[6:0]}), .sel(ULAoper));  // open: in5, in6, in7
  Negator negator_1 (.in(X), .out(negator_1_out));
  Subtractor subtractor_1 (.a(Y), .b(X), .out(subtractor_1_out));  // open: bin, bout
  nor nor_1 (Flags[0], ULAout[0], ULAout[1], ULAout[2], ULAout[3], ULAout[4], ULAout[5], ULAout[6], Flags[1]);

  assign ULAout[7] = Flags[1];
endmodule

module IDecoder (
  input  Clk,
  input  Reset,
  input  [7:0] Instr,
  input  [7:0] Flags,
  output PCinc,
  output PCload,
  output Hload,
  output MDRload,
  output MARload,
  output IRload,
  output SPinc,
  output SPdec,
  output SPload,
  output FLAGSload,
  output MEMread,
  output MEMwrite,
  output [1:0] ADDRsel,
  output DATAsel,
  output Halt,
  output [2:0] ULAoper
);

  wire and_1_out, and_2_out, and_3_out, and_4_out, and_5_out, Exec;
  wire [1:0] Conditions, JUMPsel;
  wire [2:0] uJUMP;
  wire [5:0] adder_1_out, multiplexer_1_out, uAddress, uPC_q;
  wire [18:0] uProgram_data;

  ROM #(.addrWidth(4), .dataWidth(6)) Translate (.addr(Instr[7:4]), .data(uAddress));
  and and_1 (and_1_out, ~Clk, ~Halt);  // AND_Gate
  and and_2 (and_2_out, ~Conditions[1], ~Conditions[0]);  // AND_Gate
  and and_3 (and_3_out, ~Conditions[1], Flags[0]);  // AND_Gate
  and and_4 (and_4_out, ~Conditions[0], Flags[1]);  // AND_Gate
  and and_5 (and_5_out, Flags[1], Flags[0]);
  Register #(.width(6)) uPC (.D(multiplexer_1_out), .en(1'b1), .clk(and_1_out), .Q(uPC_q), .clr(Reset));
  Multiplexer #(.select(2), .width(6)) multiplexer_1 (
    .in0(6'b001000), .in1(uPC_q), .in2(adder_1_out), .in3(uAddress), .out(multiplexer_1_out), .sel(JUMPsel));
  or or_1 (Exec, and_2_out, and_3_out, and_4_out, and_5_out);
  Adder #(.width(6)) adder_1 (.a(uPC_q), .b(6'b000001), .out(adder_1_out));  // open: cin, cout
  ROM #(.addrWidth(6), .dataWidth(22)) uProgram (.addr(uPC_q), .data({uJUMP, uProgram_data}));
  and and_6 (Conditions[0], uJUMP[0], ~uJUMP[1], uJUMP[2]);  // AND_Gate
  and and_7 (Conditions[1], ~uJUMP[0], uJUMP[1], uJUMP[2]);  // AND_Gate
  and and_8 (JUMPsel[0], uJUMP[0], ~uJUMP[2]);  // AND_Gate
  or or_2 (JUMPsel[1], uJUMP[1], uJUMP[2]);
  and and_9 (PCinc, Exec, uProgram_data[0]);
  and and_10 (PCload, Exec, uProgram_data[1]);
  and and_11 (Hload, Exec, uProgram_data[2]);
  and and_12 (MDRload, Exec, uProgram_data[3]);
  and and_13 (MARload, Exec, uProgram_data[4]);
  and and_14 (IRload, Exec, uProgram_data[5]);
  and and_15 (SPinc, Exec, uProgram_data[6]);
  and and_16 (SPdec, Exec, uProgram_data[7]);
  and and_17 (SPload, Exec, uProgram_data[8]);
  and and_18 (FLAGSload, Exec, uProgram_data[9]);
  and and_19 (MEMread, Exec, uProgram_data[10]);
  and and_20 (MEMwrite, Exec, uProgram_data[11]);
  assign ADDRsel = {2{Exec}} & uProgram_data[13:12];  // AND_Gate and_21, 2 bits wide
  and and_22 (DATAsel, Exec, uProgram_data[14]);
  and and_23 (Halt, Exec, uProgram_data[15]);
  assign ULAoper = {3{Exec}} & uProgram_data[18:16];  // AND_Gate and_24, 3 bits wide

  // Other names for the same wires on the sheet: Zin = Flags[0]; Nin = Flags[1]

  // Notes on the sheet:
  //   Endereço do FETCH = 0x08
  //   contents of Translate (hex, n*v repeats v):
  //   a b f 13 19 1f 25 2a 30 32 36 0 0 0 3a 3d
  //   Execução condicional de uInstruções
  //   Conditions Zin Nin Exec
  //          00   x   x   1
  //          01   x   0   0
  //          01   x   1   1
  //          10   0   x   0
  //          10   1   x   1
  //          11   0   x   0
  //          11   x   0   0
  //          11   1   1   1
  //   contents of uProgram (hex, n*v repeats v):
  //   8*100180 101420 180001 0 101408 100011 103408 2940 101408 100191 102408 3800 103408 104144 103408
  //   100204 100008 3800 103408 104144 103408 110204 100008 3800 103408 104144 103408 120204 100008 3800
  //   103408 104004 130204 100008 3800 103408 104144 103408 140204 100008 3800 101408 2 101408 100001
  //   280002 0 101408 300001 100002 0 103408 100180 3800 8fa0 27c690 32ae2c
endmodule

module PC (
  input  [7:0] PCin,
  input  PCload,
  input  PCinc,
  input  CLKin,
  input  Reset,
  output [7:0] PCout
);

  wire or_1_out;
  wire [7:0] adder_1_out, multiplexer_1_out;

  or or_1 (or_1_out, PCload, PCinc);
  Multiplexer #(.width(8)) multiplexer_1 (.in0(PCin), .in1(adder_1_out), .out(multiplexer_1_out), .sel(PCinc));
  Register register_1 (.D(multiplexer_1_out), .en(or_1_out), .clk(CLKin), .Q(PCout), .clr(Reset));
  Adder adder_1 (.a(PCout), .b(8'h1), .out(adder_1_out), .cin(1'b0));  // open: cout
endmodule

module SP (
  input  [7:0] SPin,
  input  SPload,
  input  Spdec,
  input  SPinc,
  input  CLKin,
  input  Reset,
  output [7:0] SPout
);

  wire [1:0] and_1_out;
  wire [7:0] adder_1_out, multiplexer_1_out, subtractor_1_out;

  Multiplexer #(.select(2), .width(8)) multiplexer_1 (
    .in1(adder_1_out), .in2(subtractor_1_out), .in3(SPin), .out(multiplexer_1_out), .sel(and_1_out));  // open: in0
  and and_1 (and_1_out[0], SPload, ~Spdec);  // AND_Gate
  and and_2 (and_1_out[1], ~SPinc, SPload);  // AND_Gate
  Register register_1 (.D(multiplexer_1_out), .en(SPload), .clk(CLKin), .Q(SPout), .clr(Reset));
  Subtractor subtractor_1 (.a(SPout), .b(8'h1), .out(subtractor_1_out));  // open: bin, bout
  Adder adder_1 (.a(8'h1), .b(SPout), .out(adder_1_out));  // open: cin, cout
endmodule

module MDR (
  input  [7:0] DataIn,
  input  [7:0] DBusIn,
  input  MEMread,
  input  MDRload,
  input  Clk,
  input  Rst,
  input  MEMwrite,
  output [7:0] DBusOut,
  output [7:0] DataOut
);

  wire [7:0] multiplexer_1_out;

  Register register_1 (.D(multiplexer_1_out), .en(MDRload), .clk(Clk), .Q(DataOut), .clr(Rst));
  Multiplexer #(.width(8)) multiplexer_1 (.in0(DataIn), .in1(DBusIn), .out(multiplexer_1_out), .sel(MEMread));
  assign DBusOut = MEMwrite ? DataOut : 8'bz;  // Controlled_Buffer controlled_buffer_1
endmodule

module MAR (
  input  [7:0] MARIn,
  input  MARload,
  input  ClkIn,
  input  Reset,
  output [7:0] MAROut
);

  Register register_1 (.D(MARIn), .en(MARload), .clk(ClkIn), .Q(MAROut), .clr(Reset));
endmodule

module H (
  input  [7:0] AccIn,
  input  ACCload,
  input  ClkIn,
  input  Reset,
  output [7:0] AccOut
);

  Register register_1 (.D(AccIn), .en(ACCload), .clk(ClkIn), .Q(AccOut), .clr(Reset));
endmodule

module IR (
  input  [7:0] IRIn,
  input  IRload,
  input  ClkIn,
  input  Reset,
  output [7:0] IROut
);

  Register register_1 (.D(IRIn), .en(IRload), .clk(ClkIn), .Q(IROut), .clr(Reset));
endmodule

module Flags (
  input  [7:0] FlagsIn,
  input  FLAGSload,
  input  Clk,
  input  Reset,
  output [7:0] FlagsOut
);

  Register Flags (.D(FlagsIn), .en(FLAGSload), .clk(Clk), .Q(FlagsOut), .clr(Reset));
  LED Z (.in(FlagsOut[0]));
  LED N (.in(FlagsOut[1]));
  LED C (.in(FlagsOut[2]));
endmodule

module MemIO (
  input  [3:0] Control,
  input  [7:0] Address,
  output [3:0] MemControl,
  output [3:0] IOControl,
  output P0,
  output P1,
  output P2,
  output P3,
  output P4,
  output P5,
  output P6,
  output P7
);

  wire [3:3] and_1_out;

  and and_1 (and_1_out[3], Address[7], Address[6], Address[5], Address[4], Address[3]);
  Decoder #(.select(3)) decoder_1 (
    .out0(P0), .out1(P1), .out2(P2), .out3(P3), .out4(P4), .out5(P5), .out6(P6), .out7(P7),
    .sel(Address[2:0]), .en(and_1_out[3]));
  assign MemControl = Control & ~{4{and_1_out[3]}};  // AND_Gate and_2, 4 bits wide
  assign IOControl = Control & {4{and_1_out[3]}};  // AND_Gate and_3, 4 bits wide
endmodule

module Computador (
);

  wire button_1_out, clock_1_out;
  wire [3:0] memio_1_memcontrol, undriven_2;
  wire [7:0] Memoria_data, undriven;

  MemIO memio_1 (
    .MemControl(memio_1_memcontrol), .Control(undriven_2), .Address(undriven));  // open: IOControl, P0, P1, P2, P3, P4, P5, P6, P7
  CPU cpu_1 (.Clock(clock_1_out), .Reset(button_1_out));
  RAM #(.asyncread("true"), .databus("bidir"), .\type ("nonvolatile")) Memoria (
    .addr(undriven), .we(memio_1_memcontrol[0]), .oe(memio_1_memcontrol[1]), .clk(memio_1_memcontrol[2]),
    .data(Memoria_data));
  Clock clock_1 (.out(clock_1_out));
  Button button_1 (.out(button_1_out));

  // Notes on the sheet:
  //   Barramento
  //   Dados
  //   Endereços
  //   Controle
endmodule
