// Logisim project SingleCycle.circ as structural Verilog: 5 circuits, main circuit RegFile
module main (
);

  wire ALUsrc, BranchZ, clk, Jal, Jr, Jump, MEMrd, MemToReg, MEMwr, PCsrc, REGwr, rst, Zero;
  wire [0:0] REGsrc;
  wire [2:0] ALUop;
  wire [4:0] multiplexer_1_out;
  wire [25:0] Bit0_25;
  wire [31:0] Abus, adder_2_out, alu_1_aluresult, bit_extender_1_out, Cbus, Jal_value, multiplexer_2_out,
       multiplexer_3_out, multiplexer_4_out, multiplexer_6_out, nextPC, PC, ram_1_dout, regfile_1_bbus,
       shifter_1_out;
  wire [31:26] Instruction;

  Button Reset (.out(rst));
  Clock clock_1 (.out(clk));
  Register #(.width(32)) u_PC (.D(nextPC), .en(1'b1), .clk(clk), .Q(PC), .clr(rst));
  ROM #(.addrWidth(12), .dataWidth(32)) rom_1 (.addr(PC[13:2]), .data({Instruction, Bit0_25}));
  ControlUnitCombinational controlunitcombinational_1 (
    .Instruction({Instruction, Bit0_25}), .Jump(Jump), .Branch(BranchZ), .MemRead(MEMrd),
    .MemToReg(MemToReg), .MemWrite(MEMwr), .ALUSrc(ALUsrc), .RegWrite(REGwr), .Jr(Jr), .ALUCtrl(ALUop),
    .RegDest({Jal, REGsrc[0]}));
  Multiplexer #(.select(2), .width(5)) multiplexer_1 (
    .in0(Bit0_25[20:16]), .in1(Bit0_25[15:11]), .in2({5{1'b1}}), .in3({5{1'b1}}), .out(multiplexer_1_out),
    .sel({Jal, REGsrc[0]}));
  RegFile regfile_1 (
    .REGwr(REGwr), .Clk(clk), .Rst(rst), .Asel(Bit0_25[25:21]), .Bsel(Bit0_25[20:16]),
    .Csel(multiplexer_1_out), .Din(Cbus), .Abus(Abus), .Bbus(regfile_1_bbus));
  assign bit_extender_1_out = {{16{Bit0_25[15]}}, Bit0_25[15:0]};  // Bit_Extender bit_extender_1
  ALU alu_1 (
    .ALUop(ALUop), .Shamt(Bit0_25[10:6]), .A(Abus), .B(multiplexer_2_out), .ALUResult(alu_1_aluresult),
    .Zero(Zero));  // open: OFlow
  Multiplexer #(.width(32)) multiplexer_2 (
    .in0(regfile_1_bbus), .in1(bit_extender_1_out), .out(multiplexer_2_out), .sel(ALUsrc));
  // Probe on PC
  Adder #(.width(32)) adder_1 (.a(PC), .b(32'h4), .out(Jal_value));  // open: cin, cout
  Shifter #(.width(32)) shifter_1 (.in(bit_extender_1_out), .\dist (5'b00010), .out(shifter_1_out));
  RAM #(.addrWidth(12), .dataWidth(32)) ram_1 (
    .addr(alu_1_aluresult[11:0]), .we(MEMwr), .oe(MEMrd), .clk(clk), .din(regfile_1_bbus), .dout(ram_1_dout));
  // Probe on {PC[31:28], Bit0_25, 2'b00}
  and and_1 (PCsrc, BranchZ, Zero);
  Adder #(.width(32)) adder_2 (.a(Jal_value), .b(shifter_1_out), .out(adder_2_out));  // open: cin, cout
  Multiplexer #(.width(32)) multiplexer_3 (.in0(Jal_value), .in1(adder_2_out), .out(multiplexer_3_out), .sel(PCsrc));
  Multiplexer #(.width(32)) multiplexer_4 (
    .in0(multiplexer_3_out), .in1({PC[31:28], Bit0_25, 2'b00}), .out(multiplexer_4_out), .sel(Jump));
  Multiplexer #(.width(32)) multiplexer_5 (.in0(multiplexer_4_out), .in1(Abus), .out(nextPC), .sel(Jr));
  Multiplexer #(.width(32)) multiplexer_6 (
    .in0(alu_1_aluresult), .in1(ram_1_dout), .out(multiplexer_6_out), .sel(MemToReg));
  Multiplexer #(.width(32)) multiplexer_7 (.in0(multiplexer_6_out), .in1(Jal_value), .out(Cbus), .sel(Jal));

  // Other names for the same wires on the sheet: Immed[15:0] = Bit0_25[15:0]; Instruction[25:0] = Bit0_25;
  //   ShAmt[4:0] = Bit0_25[10:6]; REGsrc[1] = Jal

  // Notes on the sheet:
  //   NOTA:
  //   contents of rom_1 (hex, n*v repeats v):
  //   20010008 34220005 3043ffff 612020 832822 223024 c33825 aca40064 8ca80064 22482a 225027 11050003
  //   1034022 c00000b 200b0001 200c0005 d1990095 3308cb29 f40d83e3 a4b39990 4cb2b720 f662e5f a8bed98e
  //   f226a91 36ce6f58 3224a310 fb1ab88a e3657548 f6d27c33 a753e066 3d304bb6 631f83f be59a2d1 4d03622e
  //   d9f22f2 20b3973 40022cbe 4c0647cc de3c5904 61ce806b e2255a73 8aa1ae70 ad49b3bf ed3c1d8c 3b34fa22
  //   aa89fa86 93c2261 d63912ab 149526b3 70e6c472 2f013e3d dd2a30e4 19a47309 7e5c5c7d 2f89b199 3782bfa9
  //   8b050589 29951a0a 7558a8d9 d2ae011d 5e5d67db bfb3ea0c c36b1dc 381c27a2 b8f00ef2 b6bcd0bb a628ada5
  //   82b090b0 8bd4df4a c5975285 57b1b83e 3b5858e8 a3903170 d719f842 64712ad8 9f6d9d68 de771ac7 58cd62ac
  //   929c1c37 68fcfe60 9e08fe88 1e08a10e 59e4034c 244836e5 5362ab0a 8befbf3a c7526023 f839de05 2e6f8743
  //   cdf8bebf 25bb8eff 662ba51a 2ec1948e ac2a6f5b cfe929c2 59a1a763 d44148ae 378bdaae 18be9b92 2fb29ed0
  //   71728412 c5723730 e4a0cab9 80fe121c 291c285a bac69665 8093fccd 1d8ed021 31f41319 43bc24e f5115910
  //   11194c67 5cc980dc afffe22 a6c7ad19 c4eab0fd 98c41c6b b5fd9e3e 949157b3 94d6b98c 5dee3e4e 178ab59
  //   12237e04 eabfaba8 54a52092 c90704fb 1098eef1 42350069 18f20acc 1dc3b72f b3d58c1 385a933a b77bba5e
  //   73757777 9e23b500 fd1369f0 16ef8af8 ce6b7d00 df5d0ea5 66886a1e 50b62361 18532816 69530676 70d48fa7
  //   6ebfaa77 bf7c2cd9 df1bb9ab ce257893 c66fc874 99283530 b8d2eed1 21385a26 6a71f872 b7de2dfe a05eacf1
  //   aa08b32e e2c2ee30 188b394 44c3a0f1 44074f9c 7bc41416 1aa5166 9d8ff539 1b857156 46fa6576 e1698900
  //   57297f99 e69324b 1a6a2914 f4e1d43a e6366969 2ffd73c7 fa954fe8 ba4616aa 4a25b5f1 e200ef08 ef3a7c21
  //   ff34325a 374f4b0b bb3d3b10 184ef46d 9a60b3ba 7e796007 6f27dbbc 3f8e0777 6ebcc8d7 7c0b76ce d79cae15
  //   2f9ca3b1 60a7f7cd f3154349 72e245e5 e4682753 58e2487a 69d22503 421e108d 8d53aca2 2b0ad574 3cb8170c
  //   30675115 39375675 31c1f83c a4ab3a20 96054984 826960f4 204584b3 badd5d09 27562572 5640faa3 bd0c7cc
  //   9b732741 a0a179db ebff299e 1d713d82 8d7ec9da d0f26e35 9b0a4126 29c320c 157a5aa2 a342e2c3 b42cab5b
  //   cee0c24f fd6a3d82 6002282b 5500b4b 6d4ef94 3d724026 5e971c46 bf39fb2b 6313ba7b bf2e4be2 9826c037
  //   115feae3 1d0d792e cfc9d1d3 2fe59bbe bd3be2cf 55cadcd8 b6df5545 d2cb81ce e8e42ec3 23d65a58 f4dbb854
  //   5de68a5c a4443550 c886ea31 a9372ed5 31035579 7574ff45 612253c5 398ffb76 f02deba2 2b983378 7cfc77c3
  //   94d15b23 caefcf57 84808ac5 6a1c4ddc b5342ab 116513e9 7c9f0057 cd4689bc 4485d2a3 668b8d98 8a5c4226
  //   73d91b38 1685a58a 9cc6edc 727a25c0 ece1fdc3 a245c2d e0f1e703 ba91254b be8f0b26 e8c30c4c 54bf95fb
  //   2d7a28c9 54bbc56f 7712757e fe7de971 1bb51f9d 983d4c2a 42a72051 3135b71a 73e12e4f 7bdbf0ce 568dcbb5
  //   c75aa84f f563748b 66ed1e7a 96eecc99 52784adf 55a5af6f e57788e0 239543d6 ef5edb20 77263c06 45f6d681
  //   4f194e4c 38a1b47 cd273e0e 1c733a1a b2ba934a 94dcbf9 bf62ef01 4f4af5e 8fead533 24f89a21 a3075953
  //   6ba0cee4 ce5e685d 6ed79603 799c03f7 c24d6d62 6272b43c ea118791 af985227 1417a1b 121922bf d7f2b3fd
  //   23999b64 ee80d096 587721f9 1fb6e88f b0943fbc b396f190 68521c04 9568deb8 a94b3c4b 409fd732 fd688922
  //   144b4d66 4e0e0403 cb8d5886 2b478024 43b13b99 6f74a0af 79ad027 a73e690e ed706835 95ce6034 11c7fa38
  //   1108b5fb 9471db1a 1577921a 4f4f3d96 84dfc63e 5591f371 288f194a d99ad451 b82557ca 7e428748 2eccd619
  //   837f8757 19f92ad3 f076e861 90c62c84 ecbaf172 e112bbb4 bb8ae247 f4fe2abd 961e7d74 b2623713 f35305a1
  //   bef313e6 9af93af 1e8a0c42 295d4ca 7b33531b 3198aaaa b974c1e8 9212a5a0 73a01ab6 1e4e2f12 d60f0e0
  //   ca344c9b 3ca433cd 2b0576ef 4bf78960 b0dae521 7389c1ff 86cb3417 f29ec65d bf894b19 f781ff70 3b6a19e6
  //   cd7e732e 6df819be be9e3511 6129aa2e f4d0676f 4ad943b5 a6297324 2785d6c c4625d28 a5b49860 a6c6cdff
  //   74139a3d 3dc852d a276ca74 10b0230f 78733010 c1b27dc7 86d1cbc8 8fadaa1f 3f65491b e8da8f93 f4269270
  //   e11ed6da 40230792 a4c154aa ab9d9b0a 54f14e8e 8bf54216 e5ae2e01 1e94bc57 5ceaf632 bd04136b 1c2f2b13
  //   f0de200d d0785caa 3763316e c26947bc 4db574ea e6810548 6d183f45 e0942468 710dae0c bed75696 7f78ed8
  //   24b69c6c 8e2ae37f 31f23152 c907057f c72bdeb3 9fa12817 4bfa73b9 bde17fb 93ceec9d 150a6880 a816ed08
  //   d87511aa 7524a323 7d52a793 e685853f 66451af6 99bab23e 8a9b2bea cbb89d27 bbbdb3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
  //   Apenas os bits de 2 a 13 são usados
  //   Instruction memory
  //   Data memory
endmodule

module ALU (
  input  [2:0] ALUop,
  input  [31:0] A,
  input  [31:0] B,
  input  [4:0] Shamt,
  output OFlow,
  output [31:0] ALUResult,
  output Zero
);

  wire and_2_out, and_3_out, comparator_1_lt;
  wire [31:0] adder_1_out, and_1_out, bit_extender_1_out, nor_1_out, or_1_out, shifter_1_out, shifter_2_out,
       subtractor_1_out;

  Comparator #(.width(32)) comparator_1 (.a(A), .b(B), .lt(comparator_1_lt));  // open: gt, eq
  assign bit_extender_1_out = {{31{comparator_1_lt}}, comparator_1_lt};  // Bit_Extender bit_extender_1
  Subtractor #(.width(32)) subtractor_1 (.a(A), .b(B), .out(subtractor_1_out));  // open: bin, bout
  assign nor_1_out = ~(A | B);  // NOR_Gate nor_1, 32 bits wide
  assign and_1_out = A & B;  // AND_Gate and_1, 32 bits wide
  Adder #(.width(32)) adder_1 (.a(A), .b(B), .out(adder_1_out));  // open: cin, cout
  assign or_1_out = A | B;  // OR_Gate or_1, 32 bits wide
  Shifter #(.width(32)) shifter_1 (.in(B), .\dist (Shamt), .out(shifter_1_out));
  Shifter #(.shift("lr"), .width(32)) shifter_2 (.in(B), .\dist (Shamt), .out(shifter_2_out));
  Multiplexer #(.select(3), .width(32)) multiplexer_1 (
    .in0(bit_extender_1_out), .in1(subtractor_1_out), .in2(nor_1_out), .in3(and_1_out), .in4(adder_1_out),
    .in5(or_1_out), .in6(shifter_1_out), .in7(shifter_2_out), .out(ALUResult), .sel(ALUop));
  and and_2 (and_2_out, ~ALUop[0], ~ALUop[1], ALUop[2]);  // AND_Gate
  and and_3 (and_3_out, ALUop[0], ALUop[1], ~ALUop[2]);  // AND_Gate
  Overflow overflow_1 (
    .Add(and_2_out), .Sub(and_3_out), .ASign(A[31]), .BSign(B[31]), .ResultSign(ALUResult[31]),
    .Overflow(OFlow));
  nor nor_2 (Zero, ALUResult[0], ALUResult[1], ALUResult[2], ALUResult[3], ALUResult[4], ALUResult[5], ALUResult[6], ALUResult[7], ALUResult[8], ALUResult[9], ALUResult[10], ALUResult[11], ALUResult[12], ALUResult[13], ALUResult[14], ALUResult[15], ALUResult[16], ALUResult[17], ALUResult[18], ALUResult[19], ALUResult[20], ALUResult[21], ALUResult[22], ALUResult[23], ALUResult[24], ALUResult[25], ALUResult[26], ALUResult[27], ALUResult[28], ALUResult[29], ALUResult[30], ALUResult[31]);

  // Other names for the same wires on the sheet: ASign = A[31]; ResultSign = ALUResult[31]; BSign = B[31]
endmodule

module RegFile (
  input  REGwr,
  input  [4:0] Asel,
  input  [4:0] Bsel,
  input  [4:0] Csel,
  input  [31:0] Din,
  input  Clk,
  input  Rst,
  output [31:0] Abus,
  output [31:0] Bbus
);

  wire decoder_1_out0, decoder_1_out1, decoder_1_out2, decoder_1_out3, decoder_2_out0, decoder_2_out1,
       decoder_2_out2, decoder_2_out3, decoder_2_out4, decoder_2_out5, decoder_2_out6, decoder_2_out7,
       decoder_3_out0, decoder_3_out1, decoder_3_out2, decoder_3_out3, decoder_3_out4, decoder_3_out5,
       decoder_3_out6, decoder_3_out7, decoder_4_out0, decoder_4_out1, decoder_4_out2, decoder_4_out3,
       decoder_4_out4, decoder_4_out5, decoder_4_out6, decoder_4_out7, decoder_5_out0, decoder_5_out1,
       decoder_5_out2, decoder_5_out3, decoder_5_out4, decoder_5_out5, decoder_5_out6, decoder_5_out7;
  wire [31:0] a0_q, a1_q, a2_q, a3_q, at_q, Din_t, fp_q, gp_q, k0_q, k1_q, multiplexer_1_out,
       multiplexer_2_out, multiplexer_3_out, multiplexer_4_out, multiplexer_5_out, multiplexer_6_out,
       multiplexer_7_out, multiplexer_8_out, ra_q, s0_q, s1_q, s2_q, s3_q, s4_q, s5_q, s6_q, s7_q, sp_q,
       t0_q, t1_q, t2_q, t3_q, t4_q, t5_q, t6_q, t7_q, t8_q, t9_q, v0_q, v1_q;

  Decoder #(.select(2)) decoder_1 (
    .out0(decoder_1_out0), .out1(decoder_1_out1), .out2(decoder_1_out2), .out3(decoder_1_out3),
    .sel(Csel[4:3]), .en(REGwr));
  Decoder #(.select(3)) decoder_2 (
    .out0(decoder_2_out0), .out1(decoder_2_out1), .out2(decoder_2_out2), .out3(decoder_2_out3),
    .out4(decoder_2_out4), .out5(decoder_2_out5), .out6(decoder_2_out6), .out7(decoder_2_out7),
    .sel(Csel[2:0]), .en(decoder_1_out0));
  Decoder #(.select(3)) decoder_3 (
    .out0(decoder_3_out0), .out1(decoder_3_out1), .out2(decoder_3_out2), .out3(decoder_3_out3),
    .out4(decoder_3_out4), .out5(decoder_3_out5), .out6(decoder_3_out6), .out7(decoder_3_out7),
    .sel(Csel[2:0]), .en(decoder_1_out1));
  Decoder #(.select(3)) decoder_4 (
    .out0(decoder_4_out0), .out1(decoder_4_out1), .out2(decoder_4_out2), .out3(decoder_4_out3),
    .out4(decoder_4_out4), .out5(decoder_4_out5), .out6(decoder_4_out6), .out7(decoder_4_out7),
    .sel(Csel[2:0]), .en(decoder_1_out2));
  Decoder #(.select(3)) decoder_5 (
    .out0(decoder_5_out0), .out1(decoder_5_out1), .out2(decoder_5_out2), .out3(decoder_5_out3),
    .out4(decoder_5_out4), .out5(decoder_5_out5), .out6(decoder_5_out6), .out7(decoder_5_out7),
    .sel(Csel[2:0]), .en(decoder_1_out3));
  // NoConnect on decoder_2_out0
  Register #(.width(32)) t0 (.D(Din), .en(decoder_3_out0), .clk(Clk), .Q(t0_q), .clr(Rst));
  Register #(.width(32)) s0 (.D(Din_t), .en(decoder_4_out0), .clk(Clk), .Q(s0_q), .clr(Rst));
  Register #(.width(32)) t8 (.D(Din_t), .en(decoder_5_out0), .clk(Clk), .Q(t8_q), .clr(Rst));
  Register #(.width(32)) at (.D(Din_t), .en(decoder_2_out1), .clk(Clk), .Q(at_q), .clr(Rst));
  Register #(.width(32)) t1 (.D(Din), .en(decoder_3_out1), .clk(Clk), .Q(t1_q), .clr(Rst));
  Register #(.width(32)) s1 (.D(Din_t), .en(decoder_4_out1), .clk(Clk), .Q(s1_q), .clr(Rst));
  Register #(.width(32)) t9 (.D(Din_t), .en(decoder_5_out1), .clk(Clk), .Q(t9_q), .clr(Rst));
  Register #(.width(32)) v0 (.D(Din_t), .en(decoder_2_out2), .clk(Clk), .Q(v0_q), .clr(Rst));
  Register #(.width(32)) t2 (.D(Din), .en(decoder_3_out2), .clk(Clk), .Q(t2_q), .clr(Rst));
  Register #(.width(32)) s2 (.D(Din_t), .en(decoder_4_out2), .clk(Clk), .Q(s2_q), .clr(Rst));
  Register #(.width(32)) k0 (.D(Din_t), .en(decoder_5_out2), .clk(Clk), .Q(k0_q), .clr(Rst));
  Register #(.width(32)) v1 (.D(Din_t), .en(decoder_2_out3), .clk(Clk), .Q(v1_q), .clr(Rst));
  Register #(.width(32)) t3 (.D(Din), .en(decoder_3_out3), .clk(Clk), .Q(t3_q), .clr(Rst));
  Register #(.width(32)) s3 (.D(Din_t), .en(decoder_4_out3), .clk(Clk), .Q(s3_q), .clr(Rst));
  Register #(.width(32)) k1 (.D(Din_t), .en(decoder_5_out3), .clk(Clk), .Q(k1_q), .clr(Rst));
  Register #(.width(32)) a0 (.D(Din_t), .en(decoder_2_out4), .clk(Clk), .Q(a0_q), .clr(Rst));
  Register #(.width(32)) t4 (.D(Din), .en(decoder_3_out4), .clk(Clk), .Q(t4_q), .clr(Rst));
  Register #(.width(32)) s4 (.D(Din_t), .en(decoder_4_out4), .clk(Clk), .Q(s4_q), .clr(Rst));
  Register #(.width(32)) gp (.D(Din_t), .en(decoder_5_out4), .clk(Clk), .Q(gp_q), .clr(Rst));
  Register #(.width(32)) a1 (.D(Din_t), .en(decoder_2_out5), .clk(Clk), .Q(a1_q), .clr(Rst));
  Register #(.width(32)) t5 (.D(Din), .en(decoder_3_out5), .clk(Clk), .Q(t5_q), .clr(Rst));
  Register #(.width(32)) s5 (.D(Din_t), .en(decoder_4_out5), .clk(Clk), .Q(s5_q), .clr(Rst));
  Register #(.width(32)) sp (.D(Din_t), .en(decoder_5_out5), .clk(Clk), .Q(sp_q), .clr(Rst));
  Register #(.width(32)) a2 (.D(Din_t), .en(decoder_2_out6), .clk(Clk), .Q(a2_q), .clr(Rst));
  Register #(.width(32)) t6 (.D(Din), .en(decoder_3_out6), .clk(Clk), .Q(t6_q), .clr(Rst));
  Register #(.width(32)) s6 (.D(Din_t), .en(decoder_4_out6), .clk(Clk), .Q(s6_q), .clr(Rst));
  Register #(.width(32)) fp (.D(Din_t), .en(decoder_5_out6), .clk(Clk), .Q(fp_q), .clr(Rst));
  Register #(.width(32)) a3 (.D(Din_t), .en(decoder_2_out7), .clk(Clk), .Q(a3_q), .clr(Rst));
  Register #(.width(32)) t7 (.D(Din), .en(decoder_3_out7), .clk(Clk), .Q(t7_q), .clr(Rst));
  Register #(.width(32)) s7 (.D(Din_t), .en(decoder_4_out7), .clk(Clk), .Q(s7_q), .clr(Rst));
  Register #(.width(32)) ra (.D(Din_t), .en(decoder_5_out7), .clk(Clk), .Q(ra_q), .clr(Rst));
  Multiplexer #(.select(3), .width(32)) multiplexer_1 (
    .in0({32{1'b0}}), .in1(at_q), .in2(v0_q), .in3(v1_q), .in4(a0_q), .in5(a1_q), .in6(a2_q), .in7(a3_q),
    .out(multiplexer_1_out), .sel(Asel[2:0]));
  Multiplexer #(.select(3), .width(32)) multiplexer_2 (
    .in0({32{1'b0}}), .in1(at_q), .in2(v0_q), .in3(v1_q), .in4(a0_q), .in5(a1_q), .in6(a2_q), .in7(a3_q),
    .out(multiplexer_2_out), .sel(Bsel[2:0]));
  Multiplexer #(.select(3), .width(32)) multiplexer_3 (
    .in0(t0_q), .in1(t1_q), .in2(t2_q), .in3(t3_q), .in4(t4_q), .in5(t5_q), .in6(t6_q), .in7(t7_q),
    .out(multiplexer_3_out), .sel(Asel[2:0]));
  Multiplexer #(.select(3), .width(32)) multiplexer_4 (
    .in0(t0_q), .in1(t1_q), .in2(t2_q), .in3(t3_q), .in4(t4_q), .in5(t5_q), .in6(t6_q), .in7(t7_q),
    .out(multiplexer_4_out), .sel(Bsel[2:0]));
  Multiplexer #(.select(3), .width(32)) multiplexer_5 (
    .in0(s0_q), .in1(s1_q), .in2(s2_q), .in3(s3_q), .in4(s4_q), .in5(s5_q), .in6(s6_q), .in7(s7_q),
    .out(multiplexer_5_out), .sel(Asel[2:0]));
  Multiplexer #(.select(3), .width(32)) multiplexer_6 (
    .in0(s0_q), .in1(s1_q), .in2(s2_q), .in3(s3_q), .in4(s4_q), .in5(s5_q), .in6(s6_q), .in7(s7_q),
    .out(multiplexer_6_out), .sel(Bsel[2:0]));
  Multiplexer #(.select(3), .width(32)) multiplexer_7 (
    .in0(t8_q), .in1(t9_q), .in2(k0_q), .in3(k1_q), .in4(gp_q), .in5(sp_q), .in6(fp_q), .in7(ra_q),
    .out(multiplexer_7_out), .sel(Asel[2:0]));
  Multiplexer #(.select(3), .width(32)) multiplexer_8 (
    .in0(t8_q), .in1(t9_q), .in2(k0_q), .in3(k1_q), .in4(gp_q), .in5(sp_q), .in6(fp_q), .in7(ra_q),
    .out(multiplexer_8_out), .sel(Bsel[2:0]));
  Multiplexer #(.select(2), .width(32)) multiplexer_9 (
    .in0(multiplexer_1_out), .in1(multiplexer_3_out), .in2(multiplexer_5_out), .in3(multiplexer_7_out),
    .out(Abus), .sel(Asel[4:3]));
  Multiplexer #(.select(2), .width(32)) multiplexer_10 (
    .in0(multiplexer_2_out), .in1(multiplexer_4_out), .in2(multiplexer_6_out), .in3(multiplexer_8_out),
    .out(Bbus), .sel(Bsel[4:3]));

  // Other names for the same wires on the sheet: Cbus[31:0] = Din; Clock = Clk; Reset = Rst

  // Notes on the sheet:
  //   zero
endmodule

module Overflow (
  input  Add,
  input  Sub,
  input  ASign,
  input  BSign,
  input  ResultSign,
  output Overflow
);

  wire and_1_out, and_2_out, or_1_out, xnor_1_out, xor_1_out, xor_2_out;

  xnor xnor_1 (xnor_1_out, ASign, BSign);
  xor xor_1 (xor_1_out, ASign, BSign);
  and and_1 (and_1_out, xnor_1_out, Add);
  and and_2 (and_2_out, xor_1_out, Sub);
  or or_1 (or_1_out, and_1_out, and_2_out);
  xor xor_2 (xor_2_out, ResultSign, ASign);
  and and_3 (Overflow, or_1_out, xor_2_out);

  // Notes on the sheet:
  //   Ou
  //   Overflow ocorre na adição quando ASign == BSign(B) && ResultSign != ASign
  //   Overflow ocorre na subtração (Sub==1) e ASign != BSign && ResultSign != ASign
endmodule

// Control Unit
module ControlUnitCombinational (
  input  [31:0] Instruction,
  output [2:0] ALUCtrl,
  output [1:0] RegDest,
  output Jump,
  output Branch,
  output MemRead,
  output MemToReg,
  output MemWrite,
  output ALUSrc,
  output RegWrite,
  output Jr
);

  wire and_6_out, and_7_out, and_8_out, and_10_out, and_11_out, and_12_out, and_13_out, and_14_out,
       and_15_out, and_16_out, and_17_out, and_18_out, and_19_out, and_20_out, and_21_out, and_22_out,
       and_23_out, and_24_out, and_25_out, and_26_out, and_27_out, and_28_out, and_29_out, and_30_out,
       and_31_out, and_32_out, and_33_out, and_34_out, and_35_out, and_36_out, and_37_out, not_1_out,
       not_2_out, not_3_out, not_4_out, not_5_out, not_6_out, not_7_out, not_8_out, not_9_out, not_10_out,
       not_11_out, not_12_out, not_13_out, not_14_out, not_15_out, not_16_out, not_17_out, not_18_out,
       not_19_out, not_20_out, not_21_out, not_22_out, not_23_out, not_24_out, not_25_out, not_26_out,
       not_27_out, not_28_out, not_29_out, not_30_out, not_31_out, not_32_out, not_33_out, not_34_out,
       not_35_out, not_36_out, not_37_out, not_38_out, not_39_out, not_40_out, not_41_out, not_42_out,
       not_43_out, not_44_out, not_45_out, not_46_out, not_47_out, not_48_out, not_49_out, not_50_out,
       not_51_out, not_52_out, not_53_out, not_54_out, not_55_out, not_56_out, not_57_out, not_58_out,
       not_59_out, not_60_out, not_61_out, not_62_out, not_63_out, not_64_out, not_65_out, not_66_out,
       not_67_out, not_68_out, not_69_out, not_70_out, not_71_out, not_72_out, not_73_out, not_74_out,
       not_75_out, not_76_out, not_77_out, not_78_out, not_79_out, not_80_out, not_81_out, not_82_out,
       not_83_out, not_84_out, not_85_out, not_86_out, not_87_out, not_88_out, not_89_out, not_90_out,
       not_91_out, not_92_out, not_93_out, not_94_out, not_95_out, not_96_out, not_97_out, not_98_out,
       not_99_out, not_100_out, not_101_out, not_102_out, not_103_out, not_104_out, not_105_out, not_106_out,
       not_107_out, not_108_out, not_109_out, not_110_out, not_111_out, not_112_out, not_113_out,
       not_114_out, not_115_out, not_116_out, not_117_out, not_118_out, not_119_out, not_120_out,
       not_121_out, not_122_out, not_123_out, not_124_out, not_125_out, not_126_out, not_127_out,
       not_128_out, not_129_out, not_130_out, not_131_out, not_132_out, not_133_out, not_134_out,
       not_135_out, not_136_out, not_137_out, not_138_out, not_139_out, not_140_out, not_141_out,
       not_142_out, not_143_out, not_144_out, not_145_out, not_146_out, not_147_out, not_148_out,
       not_149_out, not_150_out, not_151_out, not_152_out, not_153_out, not_154_out, not_155_out,
       not_156_out, not_157_out, not_158_out, not_159_out, not_160_out, not_161_out, not_162_out,
       not_163_out, not_164_out, not_165_out, not_166_out, not_167_out, not_168_out, not_169_out,
       not_170_out, not_171_out, not_172_out, not_173_out, not_174_out, not_175_out, not_176_out,
       not_177_out, not_178_out, not_179_out, not_180_out, not_181_out, not_182_out, not_183_out,
       not_184_out, not_185_out, not_186_out, not_187_out, not_188_out, not_189_out, not_190_out,
       not_191_out, not_192_out, not_193_out, not_194_out, not_195_out, not_196_out, not_197_out,
       not_198_out, not_199_out, not_200_out, not_201_out, not_202_out, not_203_out, not_204_out,
       not_205_out, not_206_out, not_207_out, not_208_out, not_209_out, not_210_out, not_211_out,
       not_212_out, not_213_out, not_214_out, not_215_out, not_216_out, not_217_out, not_218_out,
       not_219_out, not_220_out, not_221_out, not_222_out, not_223_out, not_224_out, not_225_out,
       not_226_out, not_227_out, not_228_out, not_229_out, not_230_out, not_231_out, not_232_out,
       not_233_out, not_234_out, not_235_out, not_236_out, not_237_out, not_238_out, not_239_out;

  not not_1 (not_1_out, Instruction[31]);
  not not_2 (not_2_out, Instruction[30]);
  not not_3 (not_3_out, Instruction[28]);
  not not_4 (not_4_out, Instruction[27]);
  not not_5 (not_5_out, Instruction[26]);
  not not_6 (not_6_out, Instruction[4]);
  not not_7 (not_7_out, Instruction[3]);
  not not_8 (not_8_out, Instruction[2]);
  not not_9 (not_9_out, Instruction[1]);
  not not_10 (not_10_out, Instruction[0]);
  not not_11 (not_11_out, Instruction[31]);
  not not_12 (not_12_out, Instruction[30]);
  not not_13 (not_13_out, Instruction[28]);
  not not_14 (not_14_out, Instruction[27]);
  not not_15 (not_15_out, Instruction[26]);
  not not_16 (not_16_out, Instruction[4]);
  not not_17 (not_17_out, Instruction[3]);
  not not_18 (not_18_out, Instruction[1]);
  not not_19 (not_19_out, Instruction[31]);
  not not_20 (not_20_out, Instruction[30]);
  not not_21 (not_21_out, Instruction[29]);
  not not_22 (not_22_out, Instruction[28]);
  not not_23 (not_23_out, Instruction[27]);
  not not_24 (not_24_out, Instruction[26]);
  not not_25 (not_25_out, Instruction[5]);
  not not_26 (not_26_out, Instruction[4]);
  not not_27 (not_27_out, Instruction[3]);
  not not_28 (not_28_out, Instruction[2]);
  not not_29 (not_29_out, Instruction[1]);
  not not_30 (not_30_out, Instruction[0]);
  not not_31 (not_31_out, Instruction[31]);
  not not_32 (not_32_out, Instruction[30]);
  not not_33 (not_33_out, Instruction[29]);
  not not_34 (not_34_out, Instruction[28]);
  not not_35 (not_35_out, Instruction[27]);
  not not_36 (not_36_out, Instruction[26]);
  not not_37 (not_37_out, Instruction[5]);
  not not_38 (not_38_out, Instruction[4]);
  not not_39 (not_39_out, Instruction[3]);
  not not_40 (not_40_out, Instruction[2]);
  not not_41 (not_41_out, Instruction[0]);
  not not_42 (not_42_out, Instruction[31]);
  not not_43 (not_43_out, Instruction[30]);
  not not_44 (not_44_out, Instruction[29]);
  not not_45 (not_45_out, Instruction[28]);
  not not_46 (not_46_out, Instruction[27]);
  not not_47 (not_47_out, Instruction[26]);
  not not_48 (not_48_out, Instruction[4]);
  not not_49 (not_49_out, Instruction[3]);
  not not_50 (not_50_out, Instruction[1]);
  not not_51 (not_51_out, Instruction[0]);
  not not_52 (not_52_out, Instruction[31]);
  not not_53 (not_53_out, Instruction[30]);
  not not_54 (not_54_out, Instruction[29]);
  not not_55 (not_55_out, Instruction[28]);
  not not_56 (not_56_out, Instruction[27]);
  not not_57 (not_57_out, Instruction[26]);
  not not_58 (not_58_out, Instruction[4]);
  not not_59 (not_59_out, Instruction[3]);
  not not_60 (not_60_out, Instruction[31]);
  not not_61 (not_61_out, Instruction[30]);
  not not_62 (not_62_out, Instruction[29]);
  not not_63 (not_63_out, Instruction[28]);
  not not_64 (not_64_out, Instruction[27]);
  not not_65 (not_65_out, Instruction[26]);
  not not_66 (not_66_out, Instruction[5]);
  not not_67 (not_67_out, Instruction[4]);
  not not_68 (not_68_out, Instruction[3]);
  not not_69 (not_69_out, Instruction[2]);
  not not_70 (not_70_out, Instruction[1]);
  not not_71 (not_71_out, Instruction[0]);
  not not_72 (not_72_out, Instruction[31]);
  not not_73 (not_73_out, Instruction[30]);
  not not_74 (not_74_out, Instruction[29]);
  not not_75 (not_75_out, Instruction[28]);
  not not_76 (not_76_out, Instruction[27]);
  not not_77 (not_77_out, Instruction[26]);
  not not_78 (not_78_out, Instruction[5]);
  not not_79 (not_79_out, Instruction[4]);
  not not_80 (not_80_out, Instruction[3]);
  not not_81 (not_81_out, Instruction[2]);
  not not_82 (not_82_out, Instruction[0]);
  not not_83 (not_83_out, Instruction[31]);
  not not_84 (not_84_out, Instruction[30]);
  not not_85 (not_85_out, Instruction[29]);
  not not_86 (not_86_out, Instruction[27]);
  not not_87 (not_87_out, Instruction[26]);
  not not_88 (not_88_out, Instruction[4]);
  not not_89 (not_89_out, Instruction[3]);
  not not_90 (not_90_out, Instruction[2]);
  not not_91 (not_91_out, Instruction[0]);
  not not_92 (not_92_out, Instruction[31]);
  not not_93 (not_93_out, Instruction[30]);
  not not_94 (not_94_out, Instruction[29]);
  not not_95 (not_95_out, Instruction[27]);
  not not_96 (not_96_out, Instruction[26]);
  not not_97 (not_97_out, Instruction[4]);
  not not_98 (not_98_out, Instruction[3]);
  not not_99 (not_99_out, Instruction[1]);
  not not_100 (not_100_out, Instruction[31]);
  not not_101 (not_101_out, Instruction[30]);
  not not_102 (not_102_out, Instruction[29]);
  not not_103 (not_103_out, Instruction[28]);
  not not_104 (not_104_out, Instruction[27]);
  not not_105 (not_105_out, Instruction[26]);
  not not_106 (not_106_out, Instruction[5]);
  not not_107 (not_107_out, Instruction[4]);
  not not_108 (not_108_out, Instruction[3]);
  not not_109 (not_109_out, Instruction[2]);
  not not_110 (not_110_out, Instruction[0]);
  not not_111 (not_111_out, Instruction[31]);
  not not_112 (not_112_out, Instruction[30]);
  not not_113 (not_113_out, Instruction[29]);
  not not_114 (not_114_out, Instruction[28]);
  not not_115 (not_115_out, Instruction[27]);
  not not_116 (not_116_out, Instruction[26]);
  not not_117 (not_117_out, Instruction[31]);
  not not_118 (not_118_out, Instruction[30]);
  not not_119 (not_119_out, Instruction[29]);
  not not_120 (not_120_out, Instruction[28]);
  not not_121 (not_121_out, Instruction[31]);
  not not_122 (not_122_out, Instruction[30]);
  not not_123 (not_123_out, Instruction[29]);
  not not_124 (not_124_out, Instruction[27]);
  not not_125 (not_125_out, Instruction[26]);
  not not_126 (not_126_out, Instruction[30]);
  not not_127 (not_127_out, Instruction[29]);
  not not_128 (not_128_out, Instruction[28]);
  not not_129 (not_129_out, Instruction[30]);
  not not_130 (not_130_out, Instruction[28]);
  not not_131 (not_131_out, Instruction[31]);
  not not_132 (not_132_out, Instruction[30]);
  not not_133 (not_133_out, Instruction[27]);
  not not_134 (not_134_out, Instruction[26]);
  not not_135 (not_135_out, Instruction[31]);
  not not_136 (not_136_out, Instruction[30]);
  not not_137 (not_137_out, Instruction[27]);
  not not_138 (not_138_out, Instruction[30]);
  not not_139 (not_139_out, Instruction[28]);
  not not_140 (not_140_out, Instruction[31]);
  not not_141 (not_141_out, Instruction[30]);
  not not_142 (not_142_out, Instruction[29]);
  not not_143 (not_143_out, Instruction[28]);
  not not_144 (not_144_out, Instruction[27]);
  not not_145 (not_145_out, Instruction[26]);
  not not_146 (not_146_out, Instruction[5]);
  not not_147 (not_147_out, Instruction[4]);
  not not_148 (not_148_out, Instruction[3]);
  not not_149 (not_149_out, Instruction[2]);
  not not_150 (not_150_out, Instruction[1]);
  not not_151 (not_151_out, Instruction[0]);
  not not_152 (not_152_out, Instruction[31]);
  not not_153 (not_153_out, Instruction[30]);
  not not_154 (not_154_out, Instruction[29]);
  not not_155 (not_155_out, Instruction[28]);
  not not_156 (not_156_out, Instruction[27]);
  not not_157 (not_157_out, Instruction[26]);
  not not_158 (not_158_out, Instruction[5]);
  not not_159 (not_159_out, Instruction[4]);
  not not_160 (not_160_out, Instruction[3]);
  not not_161 (not_161_out, Instruction[2]);
  not not_162 (not_162_out, Instruction[0]);
  not not_163 (not_163_out, Instruction[31]);
  not not_164 (not_164_out, Instruction[30]);
  not not_165 (not_165_out, Instruction[29]);
  not not_166 (not_166_out, Instruction[28]);
  not not_167 (not_167_out, Instruction[27]);
  not not_168 (not_168_out, Instruction[26]);
  not not_169 (not_169_out, Instruction[5]);
  not not_170 (not_170_out, Instruction[4]);
  not not_171 (not_171_out, Instruction[2]);
  not not_172 (not_172_out, Instruction[1]);
  not not_173 (not_173_out, Instruction[0]);
  not not_174 (not_174_out, Instruction[31]);
  not not_175 (not_175_out, Instruction[30]);
  not not_176 (not_176_out, Instruction[29]);
  not not_177 (not_177_out, Instruction[28]);
  not not_178 (not_178_out, Instruction[31]);
  not not_179 (not_179_out, Instruction[30]);
  not not_180 (not_180_out, Instruction[28]);
  not not_181 (not_181_out, Instruction[27]);
  not not_182 (not_182_out, Instruction[26]);
  not not_183 (not_183_out, Instruction[31]);
  not not_184 (not_184_out, Instruction[30]);
  not not_185 (not_185_out, Instruction[27]);
  not not_186 (not_186_out, Instruction[30]);
  not not_187 (not_187_out, Instruction[28]);
  not not_188 (not_188_out, Instruction[31]);
  not not_189 (not_189_out, Instruction[30]);
  not not_190 (not_190_out, Instruction[27]);
  not not_191 (not_191_out, Instruction[26]);
  not not_192 (not_192_out, Instruction[31]);
  not not_193 (not_193_out, Instruction[30]);
  not not_194 (not_194_out, Instruction[27]);
  not not_195 (not_195_out, Instruction[26]);
  not not_196 (not_196_out, Instruction[31]);
  not not_197 (not_197_out, Instruction[30]);
  not not_198 (not_198_out, Instruction[27]);
  and and_1 (RegDest[0], not_111_out, not_112_out, not_113_out, not_114_out, not_115_out, not_116_out);
  and and_2 (Jump, not_117_out, not_118_out, not_119_out, not_120_out, Instruction[27]);
  and and_3 (Branch, not_121_out, not_122_out, not_123_out, Instruction[28], not_124_out, not_125_out);
  and and_4 (MemRead, Instruction[31], not_126_out, not_127_out, not_128_out, Instruction[27], Instruction[26]);
  and and_5 (MemWrite, Instruction[31], not_129_out, Instruction[29], not_130_out, Instruction[27], Instruction[26]);
  and and_6 (and_6_out, not_131_out, not_132_out, Instruction[29], not_133_out, not_134_out);
  and and_7 (and_7_out, not_135_out, not_136_out, Instruction[29], Instruction[28], not_137_out);
  and and_8 (and_8_out, Instruction[31], not_138_out, not_139_out, Instruction[27], Instruction[26]);
  not not_199 (not_199_out, Instruction[31]);
  not not_200 (not_200_out, Instruction[30]);
  not not_201 (not_201_out, Instruction[28]);
  not not_202 (not_202_out, Instruction[27]);
  not not_203 (not_203_out, Instruction[26]);
  not not_204 (not_204_out, Instruction[3]);
  not not_205 (not_205_out, Instruction[31]);
  not not_206 (not_206_out, Instruction[30]);
  not not_207 (not_207_out, Instruction[28]);
  not not_208 (not_208_out, Instruction[27]);
  not not_209 (not_209_out, Instruction[26]);
  not not_210 (not_210_out, Instruction[31]);
  not not_211 (not_211_out, Instruction[30]);
  not not_212 (not_212_out, Instruction[28]);
  not not_213 (not_213_out, Instruction[27]);
  not not_214 (not_214_out, Instruction[26]);
  not not_215 (not_215_out, Instruction[31]);
  not not_216 (not_216_out, Instruction[30]);
  not not_217 (not_217_out, Instruction[28]);
  not not_218 (not_218_out, Instruction[27]);
  not not_219 (not_219_out, Instruction[26]);
  not not_220 (not_220_out, Instruction[31]);
  not not_221 (not_221_out, Instruction[30]);
  not not_222 (not_222_out, Instruction[28]);
  not not_223 (not_223_out, Instruction[27]);
  not not_224 (not_224_out, Instruction[26]);
  not not_225 (not_225_out, Instruction[31]);
  not not_226 (not_226_out, Instruction[30]);
  not not_227 (not_227_out, Instruction[28]);
  not not_228 (not_228_out, Instruction[27]);
  not not_229 (not_229_out, Instruction[26]);
  not not_230 (not_230_out, Instruction[30]);
  not not_231 (not_231_out, Instruction[29]);
  not not_232 (not_232_out, Instruction[28]);
  not not_233 (not_233_out, Instruction[31]);
  not not_234 (not_234_out, Instruction[30]);
  not not_235 (not_235_out, Instruction[27]);
  not not_236 (not_236_out, Instruction[26]);
  not not_237 (not_237_out, Instruction[31]);
  not not_238 (not_238_out, Instruction[30]);
  not not_239 (not_239_out, Instruction[27]);
  and and_9 (RegDest[1], not_174_out, not_175_out, not_176_out, not_177_out, Instruction[27], Instruction[26]);
  and and_10 (and_10_out, not_1_out, not_2_out, not_3_out, not_4_out, not_5_out, Instruction[5], not_6_out, not_7_out, not_8_out, not_9_out, not_10_out);
  and and_11 (and_11_out, not_11_out, not_12_out, not_13_out, not_14_out, not_15_out, Instruction[5], not_16_out, not_17_out, Instruction[2], not_18_out, Instruction[0]);
  and and_12 (and_12_out, not_19_out, not_20_out, not_21_out, not_22_out, not_23_out, not_24_out, not_25_out, not_26_out, not_27_out, not_28_out, not_29_out, not_30_out);
  and and_13 (and_13_out, not_31_out, not_32_out, not_33_out, not_34_out, not_35_out, not_36_out, not_37_out, not_38_out, not_39_out, not_40_out, Instruction[1], not_41_out);
  and and_14 (and_14_out, not_178_out, not_179_out, Instruction[29], not_180_out, not_181_out, not_182_out);
  and and_15 (and_15_out, not_183_out, not_184_out, Instruction[29], Instruction[28], not_185_out, Instruction[26]);
  and and_16 (and_16_out, Instruction[31], not_186_out, not_187_out, Instruction[27], Instruction[26]);
  and and_17 (and_17_out, not_42_out, not_43_out, not_44_out, not_45_out, not_46_out, not_47_out, Instruction[5], not_48_out, not_49_out, Instruction[2], not_50_out, not_51_out);
  and and_18 (and_18_out, not_52_out, not_53_out, not_54_out, not_55_out, not_56_out, not_57_out, Instruction[5], not_58_out, not_59_out, Instruction[2], Instruction[1], Instruction[0]);
  and and_19 (and_19_out, not_60_out, not_61_out, not_62_out, not_63_out, not_64_out, not_65_out, not_66_out, not_67_out, not_68_out, not_69_out, not_70_out, not_71_out);
  and and_20 (and_20_out, not_72_out, not_73_out, not_74_out, not_75_out, not_76_out, not_77_out, not_78_out, not_79_out, not_80_out, not_81_out, Instruction[1], not_82_out);
  and and_21 (and_21_out, not_188_out, not_189_out, Instruction[29], Instruction[28], not_190_out, not_191_out);
  and and_22 (and_22_out, not_83_out, not_84_out, not_85_out, not_86_out, not_87_out, Instruction[5], not_88_out, not_89_out, not_90_out, Instruction[1], not_91_out);
  and and_23 (and_23_out, not_92_out, not_93_out, not_94_out, not_95_out, not_96_out, Instruction[5], not_97_out, not_98_out, Instruction[2], not_99_out);
  and and_24 (and_24_out, not_100_out, not_101_out, not_102_out, not_103_out, not_104_out, not_105_out, not_106_out, not_107_out, not_108_out, not_109_out, Instruction[1], not_110_out);
  and and_25 (and_25_out, not_192_out, not_193_out, Instruction[28], not_194_out, not_195_out);
  and and_26 (and_26_out, not_196_out, not_197_out, Instruction[29], Instruction[28], not_198_out);
  or or_1 (ALUSrc, and_6_out, and_7_out, and_8_out);
  and and_27 (and_27_out, not_199_out, not_200_out, not_201_out, not_202_out, not_203_out, not_204_out);
  and and_28 (and_28_out, not_205_out, not_206_out, not_207_out, not_208_out, not_209_out, Instruction[0]);
  and and_29 (and_29_out, not_210_out, not_211_out, not_212_out, not_213_out, not_214_out, Instruction[1]);
  and and_30 (and_30_out, not_215_out, not_216_out, not_217_out, not_218_out, not_219_out, Instruction[2]);
  and and_31 (and_31_out, not_220_out, not_221_out, not_222_out, not_223_out, not_224_out, Instruction[4]);
  and and_32 (and_32_out, not_225_out, not_226_out, not_227_out, not_228_out, not_229_out, Instruction[5]);
  and and_33 (and_33_out, not_230_out, not_231_out, not_232_out, Instruction[27], Instruction[26]);
  and and_34 (and_34_out, not_233_out, not_234_out, Instruction[29], not_235_out, not_236_out);
  and and_35 (and_35_out, not_237_out, not_238_out, Instruction[29], Instruction[28], not_239_out);
  and and_36 (and_36_out, not_140_out, not_141_out, not_142_out, not_143_out, not_144_out, not_145_out, not_146_out, not_147_out, not_148_out, not_149_out, not_150_out, not_151_out);
  and and_37 (and_37_out, not_152_out, not_153_out, not_154_out, not_155_out, not_156_out, not_157_out, not_158_out, not_159_out, not_160_out, not_161_out, Instruction[1], not_162_out);
  and and_38 (Jr, not_163_out, not_164_out, not_165_out, not_166_out, not_167_out, not_168_out, not_169_out, not_170_out, Instruction[3], not_171_out, not_172_out, not_173_out);
  or or_2 (ALUCtrl[2], and_10_out, and_11_out, and_12_out, and_13_out, and_14_out, and_15_out, and_16_out);
  or or_3 (ALUCtrl[1], and_17_out, and_18_out, and_19_out, and_20_out, and_21_out);
  or or_4 (ALUCtrl[0], and_22_out, and_23_out, and_24_out, and_25_out, and_26_out);
  or or_5 (RegWrite, and_27_out, and_28_out, and_29_out, and_30_out, and_31_out, and_32_out, and_33_out, and_34_out, and_35_out, and_36_out, and_37_out);

  assign MemToReg = MemRead;

  // Other names for the same wires on the sheet: ALU0 = ALUCtrl[0]; ALU1 = ALUCtrl[1]; ALU2 = ALUCtrl[2];
  //   Bit0_5[5:0] = Instruction[5:0]; Bit26_31[5:0] = Instruction[31:26]; RegDest_t = RegDest[0]; Jal = RegDest[1]

  // Notes on the sheet:
  //   MemRead e MemToReg estão conectados porque os sinais são emitidos sempre juntos
endmodule
