// Logisim project UNUS-8S.v1.circ as structural Verilog: 4 circuits, main circuit CPUv2
module CPUv2 (
);

  wire clk, decoder_1_out1, decoder_1_out2, decoder_1_out3, decoder_1_out4, decoder_1_out5, decoder_1_out6,
       decoder_1_out7, MClock, MEMrd, MEMwr, MReset, or_1_out, REGwr, rst;
  wire [2:0] ALUop, Asel, Bsel, Csel;
  wire [3:0] Flags;
  wire [7:0] ACC_q, BP_q, CBus, Instr, MAR_q, MDR_q, multiplexer_1_out, multiplexer_2_out, multiplexer_3_out,
       PC_q, ram_1_data, SP_q;

  Decoder #(.select(3)) decoder_1 (
    .out1(decoder_1_out1), .out2(decoder_1_out2), .out3(decoder_1_out3), .out4(decoder_1_out4),
    .out5(decoder_1_out5), .out6(decoder_1_out6), .out7(decoder_1_out7), .sel(Csel), .en(REGwr));  // open: out0
  Clock clock_1 (.out(clk));
  Button Reset (.out(rst));
  Register SP (.D(CBus), .en(decoder_1_out7), .clk(MClock), .Q(SP_q), .clr(MReset));
  Register BP (.D(CBus), .en(decoder_1_out6), .clk(MClock), .Q(BP_q), .clr(MReset));
  CTRLv4 ctrlv4_1 (
    .IRin(Instr), .FLAGSin(Flags), .Clk(clk), .Rst(rst), .MEMrd(MEMrd), .MEMwr(MEMwr), .REGwr(REGwr),
    .Asel(Asel), .Bsel(Bsel), .Csel(Csel), .ALUop(ALUop), .MClock(MClock), .MReset(MReset));
  Register ACC (.D(CBus), .en(decoder_1_out5), .clk(MClock), .Q(ACC_q), .clr(MReset));
  Register PC (.D(CBus), .en(decoder_1_out4), .clk(MClock), .Q(PC_q), .clr(MReset));
  Register IR (.D(CBus), .en(decoder_1_out3), .clk(MClock), .Q(Instr), .clr(MReset));
  RAM #(.asyncread("true"), .databus("bidir"), .\type ("nonvolatile")) ram_1 (
    .addr(MAR_q), .we(MEMwr), .oe(MEMrd), .clk(MClock), .data(ram_1_data));
  Register MAR (.D(CBus), .en(decoder_1_out2), .clk(MClock), .Q(MAR_q), .clr(MReset));
  or or_1 (or_1_out, decoder_1_out1, MEMrd);
  Multiplexer #(.width(8)) multiplexer_1 (.in0(CBus), .in1(ram_1_data), .out(multiplexer_1_out), .sel(MEMrd));
  Register MDR (.D(multiplexer_1_out), .en(or_1_out), .clk(MClock), .Q(MDR_q), .clr(MReset));
  Multiplexer #(.select(3), .width(8)) multiplexer_2 (
    .in0({8{1'b0}}), .in1(MDR_q), .in2(MAR_q), .in3(Instr), .in4(PC_q), .in5(ACC_q), .in6(BP_q), .in7(SP_q),
    .out(multiplexer_2_out), .sel(Asel));
  Multiplexer #(.select(3), .width(8)) multiplexer_3 (
    .in0({8{1'b0}}), .in1(MDR_q), .in2(MAR_q), .in3(Instr), .in4(PC_q), .in5(ACC_q), .in6(BP_q), .in7(SP_q),
    .out(multiplexer_3_out), .sel(Bsel));
  assign ram_1_data = MEMwr ? MDR_q : 8'bz;  // Controlled_Buffer controlled_buffer_1
  ALU alu_1 (.Bbus(multiplexer_3_out), .ALUop(ALUop), .Abus(multiplexer_2_out), .Cbus(CBus), .FLAGSout(Flags));
endmodule

module CTRLv4 (
  input  [3:0] FLAGSin,
  input  [7:0] IRin,
  input  Clk,
  input  Rst,
  output MClock,
  output MReset,
  output MEMrd,
  output MEMwr,
  output REGwr,
  output [2:0] Asel,
  output [2:0] Bsel,
  output [2:0] Csel,
  output [2:0] ALUop
);

  wire clkrst_1_iclock, Exec, FLAGSwr, Halt, multiplexer_2_out;
  wire [1:0] uPCsel;
  wire [2:0] uJump;
  wire [3:0] FLAGS_q;
  wire [6:0] adder_1_out, multiplexer_1_out, Translator_out, uPC_q;
  wire [16:0] uCodigo_data;

  PLA #(.in_width(8), .out_width(7), .\table ("00000000 0000100 # NOP\n00010000 0001101 # LD\n00010001 0000101 # LDX\n00010010 0010011 # LDI\n00100000 0011110 # ST\n00100001 0010111 # STX\n00110011 0100011 # PUSH\n01000011 0100111 # POP\n01010000 0101011 # JUMP\n01010001 0101111 # JN\n01010010 0110011 # JZ\n01010100 0111001 # JC\n01011000 0111101 # JV\n01100000 1000010 # CALL\n01100001 1001010 # RET\n10000000 1001110 # ADD\n10000010 1010100 # ADDI\n10010000 1011001 # AND\n10010010 1011111 # ANDI\n10110000 1100100 # OR\n11000011 1101010 # NOT\n10010000 1011000 # INC\n11010011 1101011 # SRL\n11100011 1101100 # SLL\n11110011 1101101 # SRA\n11111111 1101110 # HALT")) Translator (
    .in(IRin), .out(Translator_out));
  Register #(.width(4)) FLAGS (.D(FLAGSin), .en(FLAGSwr), .clk(MClock), .Q(FLAGS_q), .clr(MReset));
  LED N (.in(FLAGS_q[0]));
  Multiplexer #(.select(2), .width(7)) multiplexer_1 (
    .in0(adder_1_out), .in1({7{1'b0}}), .in2(Translator_out), .out(multiplexer_1_out), .sel(uPCsel));  // open: in3
  LED Z (.in(FLAGS_q[1]));
  LED C (.in(FLAGS_q[2]));
  LED V (.in(FLAGS_q[3]));
  Multiplexer #(.select(2)) multiplexer_2 (
    .in0(FLAGS_q[0]), .in1(FLAGS_q[1]), .in2(FLAGS_q[2]), .in3(FLAGS_q[3]), .out(multiplexer_2_out),
    .sel(uJump[1:0]));
  Register #(.width(7)) uPC (.D(multiplexer_1_out), .en(1'b1), .clk(clkrst_1_iclock), .Q(uPC_q), .clr(MReset));
  ClkRst clkrst_1 (.Halt(Halt), .Clk(Clk), .Rst(Rst), .Mclock(MClock), .MReset(MReset), .iClock(clkrst_1_iclock));
  or or_1 (Exec, multiplexer_2_out, uJump[2]);
  Multiplexer #(.width(2)) multiplexer_3 (.in0(uJump[1:0]), .in1(2'b00), .out(uPCsel), .sel(uJump[2]));
  Adder #(.width(7)) adder_1 (.a(7'b0000001), .b(uPC_q), .out(adder_1_out));  // open: cin, cout
  ROM #(.addrWidth(7), .dataWidth(20)) uCodigo (.addr(uPC_q), .data({uJump, uCodigo_data}));
  assign {ALUop, Csel, Bsel, Asel, REGwr, MEMwr, MEMrd} = Exec ? uCodigo_data[14:0] : 15'bz;  // Controlled_Buffer controlled_buffer_1
  Pull_Resistor pull_resistor_1 (.node({ALUop, Csel, Bsel, Asel, REGwr, MEMwr, MEMrd}));
  assign {FLAGSwr, Halt} = Exec ? uCodigo_data[16:15] : 2'bz;  // Controlled_Buffer controlled_buffer_2
  Pull_Resistor pull_resistor_2 (.node({FLAGSwr, Halt}));

  // Other names for the same wires on the sheet: Clk_t = MClock; Rst_t = MReset

  // Notes on the sheet:
  //   contents of uCodigo (hex, n*v repeats v):
  //   810dc 80001 8144c e461c c0000 810dc 80001 8104c 80001 8104c 80001 8184c c461c 810dc 80001 8104c
  //   80001 8184c c461c 810dc 80001 8184c c461c 810dc 80001 8104c 80001 8104c 81122 c461c 810dc 80001
  //   8104c 81122 c461c 83e2c 80bb4 811b4 c1122 811b4 80001 8184c 84c34 810dc 80001 c164c 810dc 80001
  //   8461c 164c c0000 810dc 80001 8461c 2164c c0000 810dc 80001 8461c 4164c c0000 810dc 80001 8461c 6164c
  //   c0000 810dc 80001 8461c 83e2c 80bb4 811b4 81122 c164c 811b4 80001 8164c c4c34 810dc 80001 8104c
  //   80001 90864 c461c 810dc 80001 90864 c461c d4824 810dc 80001 8104c 80001 91864 c461c 810dc 8104c
  //   80001 91864 c461c 810dc 80001 8104c 80001 92864 c461c d3824 d5824 d5824 d5824 a8000
  //   Next      000
  //   Fetch     001
  //   Dispatch  010
  //   N.U.      011
  //   CondN     100
  //   CondZ     101
  //   CondC     110
  //   CondV     111
endmodule

module ALU (
  input  [7:0] Abus,
  input  [7:0] Bbus,
  input  [2:0] ALUop,
  output [7:0] Cbus,
  output [3:0] FLAGSout
);

  wire adder_1_cout, adder_2_cout;
  wire [6:0] adder_1_out;
  wire [7:0] and_1_out, multiplexer_1_out, not_1_out, or_1_out, shifter_1_out, shifter_2_out, shifter_3_out;
  wire [7:7] adder_2_out;

  Multiplexer #(.width(8)) multiplexer_1 (.in0(Bbus), .in1({8{1'b0}}), .out(multiplexer_1_out), .sel(ALUop[2]));
  Adder #(.width(7)) adder_1 (
    .a(Abus[6:0]), .b(multiplexer_1_out[6:0]), .out(adder_1_out), .cin(ALUop[2]), .cout(adder_1_cout));
  Adder #(.width(1)) adder_2 (
    .a(Abus[7]), .b(multiplexer_1_out[7]), .out(adder_2_out[7]), .cin(adder_1_cout), .cout(adder_2_cout));
  assign and_1_out = Abus & Bbus;  // AND_Gate and_1, 8 bits wide
  assign or_1_out = Abus | Bbus;  // OR_Gate or_1, 8 bits wide
  assign not_1_out = ~Abus;  // NOT_Gate not_1, 8 bits wide
  Shifter #(.shift("lr")) shifter_1 (.in(Abus), .\dist (3'b001), .out(shifter_1_out));
  Shifter shifter_2 (.in(Abus), .\dist (3'b001), .out(shifter_2_out));
  Shifter #(.shift("ar")) shifter_3 (.in(Abus), .\dist (3'b001), .out(shifter_3_out));
  xor xor_1 (FLAGSout[3], adder_1_cout, adder_2_cout);
  Multiplexer #(.select(3)) multiplexer_2 (
    .in0(adder_2_cout), .in1(1'b0), .in2(1'b0), .in3(1'b0), .in4(adder_2_cout), .in5(Abus[0]), .in6(Abus[7]),
    .in7(Abus[0]), .out(FLAGSout[2]), .sel(ALUop));
  Multiplexer #(.select(3), .width(8)) multiplexer_3 (
    .in0({adder_2_out[7], adder_1_out}), .in1(and_1_out), .in2(or_1_out), .in3(not_1_out),
    .in4({adder_2_out[7], adder_1_out}), .in5(shifter_1_out), .in6(shifter_2_out), .in7(shifter_3_out),
    .out(Cbus), .sel(ALUop));
  nor nor_1 (FLAGSout[1], Cbus[0], Cbus[1], Cbus[2], Cbus[3], Cbus[4], Cbus[5], Cbus[6], Cbus[7]);

  assign FLAGSout[0] = Cbus[7];

  // Other names for the same wires on the sheet: inc = ALUop[2]; N = Cbus[7]; Z = FLAGSout[1]; C = FLAGSout[2];
  //   V = FLAGSout[3]
endmodule

module ClkRst (
  input  Clk,
  input  Halt,
  input  Rst,
  output iClock,
  output Mclock,
  output MReset
);

  wire d_ff_1_q, por_1_out;

  POR por_1 (.out(por_1_out));
  D_Flip_Flop d_ff_1 (.D(1'b1), .clk(Clk), .Q(d_ff_1_q), .reset(MReset));  // open: Qn, preset
  or or_1 (MReset, Rst, por_1_out);
  and and_1 (iClock, ~Mclock, ~Halt);  // AND_Gate
  and and_2 (Mclock, Clk, d_ff_1_q);
endmodule
