// Logisim project UNUS-8v1.circ as structural Verilog: 6 circuits, main circuit CPUv1
module CPUv1 (
);

  wire clk, IRwr, MARwr, MDRwr, MEMrd, MEMwr, or_1_out, PCinc, rst;
  wire [7:0] adder_1_out, controlled_buffer_1_out, iData, Instr, MAR_q, MDR_q, multiplexer_1_out, PC_q;

  Register PC (.D(adder_1_out), .en(PCinc), .clk(clk), .Q(PC_q), .clr(rst));
  Adder adder_1 (.a(8'h1), .b(PC_q), .out(adder_1_out));  // open: cin, cout
  Register IR (.D(MDR_q), .en(IRwr), .clk(clk), .Q(Instr), .clr(rst));
  Register MAR (.D(PC_q), .en(MARwr), .clk(clk), .Q(MAR_q), .clr(rst));
  CTRLv1 ctrlv1_1 (
    .Instr(Instr), .clk(clk), .rst(rst), .MARwr(MARwr), .MDRwr(MDRwr), .MEMrd(MEMrd), .MEMwr(MEMwr),
    .PCinc(PCinc), .IRwr(IRwr));
  Multiplexer #(.width(8)) multiplexer_1 (
    .in0(iData), .in1(controlled_buffer_1_out), .out(multiplexer_1_out), .sel(MEMrd));
  Register MDR (.D(multiplexer_1_out), .en(or_1_out), .clk(clk), .Q(MDR_q), .clr(rst));
  or or_1 (or_1_out, MDRwr, MEMrd);
  assign controlled_buffer_1_out = MEMwr ? MDR_q : 8'bz;  // Controlled_Buffer controlled_buffer_1
  Clock clock_1 (.out(clk));
  Button Reset (.out(rst));
  RAM #(.asyncread("true"), .databus("bidir"), .\type ("nonvolatile")) ram_1 (
    .addr(MAR_q), .we(MEMwr), .oe(MEMrd), .clk(clk), .data(controlled_buffer_1_out));
endmodule

module CPUv2 (
);

  wire clk, decoder_1_out1, decoder_1_out2, decoder_1_out3, decoder_1_out4, decoder_1_out5, decoder_1_out6,
       decoder_1_out7, MEMrd, MEMwr, or_1_out, REGwr, rst;
  wire [2:0] ALUop, Asel, Bsel, Csel;
  wire [3:0] Flags;
  wire [7:0] ABus, ACC_q, AUX_q, BBus, CBus, Instr, MAR_q, MDR_q, multiplexer_1_out, PC_q, ram_1_data, SP_q;

  Decoder #(.select(3)) decoder_1 (
    .out1(decoder_1_out1), .out2(decoder_1_out2), .out3(decoder_1_out3), .out4(decoder_1_out4),
    .out5(decoder_1_out5), .out6(decoder_1_out6), .out7(decoder_1_out7), .sel(Csel), .en(REGwr));  // open: out0
  Clock clock_1 (.out(clk));
  Button Reset (.out(rst));
  Register SP (.D(CBus), .en(decoder_1_out7), .clk(clk), .Q(SP_q), .clr(rst));
  Register AUX (.D(CBus), .en(decoder_1_out6), .clk(clk), .Q(AUX_q), .clr(rst));
  CTRLv3 ctrlv3_1 (
    .Instr(Instr), .clk(clk), .rst(rst), .Flags(Flags), .MEMrd(MEMrd), .MEMwr(MEMwr), .REGwr(REGwr),
    .Asel(Asel), .Bsel(Bsel), .Csel(Csel), .ALUop(ALUop));
  Register ACC (.D(CBus), .en(decoder_1_out5), .clk(clk), .Q(ACC_q), .clr(rst));
  Register PC (.D(CBus), .en(decoder_1_out4), .clk(clk), .Q(PC_q), .clr(rst));
  ALU alu_1 (.Bbus(BBus), .ALUop(ALUop), .Abus(ABus), .Cbus(CBus), .FLAGSout(Flags));
  Register IR (.D(CBus), .en(decoder_1_out3), .clk(clk), .Q(Instr), .clr(rst));
  RAM #(.asyncread("true"), .databus("bidir"), .\type ("nonvolatile")) ram_1 (
    .addr(MAR_q), .we(MEMwr), .oe(MEMrd), .clk(clk), .data(ram_1_data));
  Register MAR (.D(CBus), .en(decoder_1_out2), .clk(clk), .Q(MAR_q), .clr(rst));
  or or_1 (or_1_out, decoder_1_out1, MEMrd);
  Multiplexer #(.width(8)) multiplexer_1 (.in0(CBus), .in1(ram_1_data), .out(multiplexer_1_out), .sel(MEMrd));
  Register MDR (.D(multiplexer_1_out), .en(or_1_out), .clk(clk), .Q(MDR_q), .clr(rst));
  Multiplexer #(.select(3), .width(8)) multiplexer_2 (
    .in0({8{1'b0}}), .in1(MDR_q), .in2(MAR_q), .in3(Instr), .in4(PC_q), .in5(ACC_q), .in6(AUX_q), .in7(SP_q),
    .out(ABus), .sel(Asel));
  Multiplexer #(.select(3), .width(8)) multiplexer_3 (
    .in0({8{1'b0}}), .in1(MDR_q), .in2(MAR_q), .in3(Instr), .in4(PC_q), .in5(ACC_q), .in6(AUX_q), .in7(SP_q),
    .out(BBus), .sel(Bsel));
  assign ram_1_data = MEMwr ? MDR_q : 8'bz;  // Controlled_Buffer controlled_buffer_1
endmodule

module CTRLv1 (
  input  [7:0] Instr,
  input  clk,
  input  rst,
  output MARwr,
  output MDRwr,
  output MEMrd,
  output MEMwr,
  output PCinc,
  output IRwr
);

  wire pull_resistor_1_node;
  wire [1:0] register_1_q, rom_1_data;

  ROM #(.addrWidth(2)) rom_1 (.addr(register_1_q), .data({MARwr, MDRwr, MEMrd, MEMwr, PCinc, IRwr, rom_1_data}));
  Register #(.width(2)) register_1 (.D(rom_1_data), .en(pull_resistor_1_node), .clk(clk), .Q(register_1_q), .clr(rst));
  Pull_Resistor #(.pull(1)) pull_resistor_1 (.node(pull_resistor_1_node));

  // Notes on the sheet:
  //   contents of rom_1 (hex, n*v repeats v):
  //   81 2a 4
  //   Atual MARwr MDRwr MEMrd MEMwr PCinc IRwr Prox HEXA
  //     00    1     0     0     0     0     0   01   81
  //     01    0     0     1     0     1     0   10   2A
  //     10    0     0     0     0     0     1   00   04
endmodule

module CTRLv2 (
  input  [7:0] Instr,
  input  clk,
  input  rst,
  output MARwr,
  output MDRwr,
  output MEMrd,
  output MEMwr,
  output PCinc,
  output IRwr
);

  wire decoder_1_out0, decoder_1_out1, decoder_1_out2, decoder_1_out3, pull_resistor_1_node;
  wire [1:0] register_1_q;
  wire [10:0] rom_1_data;

  ROM #(.addrWidth(4), .dataWidth(11)) rom_1 (
    .addr({Instr[1:0], register_1_q}),
    .data({rom_1_data[10:8], MARwr, MDRwr, MEMrd, MEMwr, PCinc, IRwr, rom_1_data[1:0]}));
  Register #(.width(2)) register_1 (
    .D(rom_1_data[1:0]), .en(pull_resistor_1_node), .clk(clk), .Q(register_1_q), .clr(rst));
  Pull_Resistor #(.pull(1)) pull_resistor_1 (.node(pull_resistor_1_node));
  Decoder #(.select(2)) decoder_1 (
    .out0(decoder_1_out0), .out1(decoder_1_out1), .out2(decoder_1_out2), .out3(decoder_1_out3),
    .sel(rom_1_data[9:8]), .en(rom_1_data[10]));
  LED L3 (.in(decoder_1_out3));
  LED L2 (.in(decoder_1_out2));
  LED L1 (.in(decoder_1_out1));
  LED L0 (.in(decoder_1_out0));

  // Notes on the sheet:
  //   contents of rom_1 (hex, n*v repeats v):
  //   81 2a 7 404 81 2a 7 504 81 2a 7 604 81 2a 7 704
  //   Instr Atual Enb LED# MARwr MDRwr MEMrd MEMwr PCinc IRwr Prox HEXA
  //     00    00   0   00    1     0     0     0     0     0   01   081
  //     00    01   0   00    0     0     1     0     1     0   10   02A
  //     00    10   0   00    0     0     0     0     0     1   11   007
  //     00    10   1   00    0     0     0     0     0     1   00   404
  //     01    00   0   00    1     0     0     0     0     0   01   081
  //     01    01   0   00    0     0     1     0     1     0   10   02A
  //     01    10   0   00    0     0     0     0     0     1   11   007
  //     01    10   1   01    0     0     0     0     0     1   00   504
  //     10    00   0   00    1     0     0     0     0     0   01   081
  //     10    01   0   00    0     0     1     0     1     0   10   02A
  //     10    10   0   00    0     0     0     0     0     1   11   007
  //     10    10   1   10    0     0     0     0     0     1   00   604
  //     11    00   0   00    1     0     0     0     0     0   01   081
  //     11    01   0   00    0     0     1     0     1     0   10   02A
  //     11    10   0   00    0     0     0     0     0     1   11   007
  //     11    10   1   11    0     0     0     0     0     1   00   704
endmodule

module CTRLv3 (
  input  [7:0] Instr,
  input  [3:0] Flags,
  input  clk,
  input  rst,
  output MEMrd,
  output MEMwr,
  output REGwr,
  output [2:0] Asel,
  output [2:0] Bsel,
  output [2:0] Csel,
  output [2:0] ALUop
);

  wire pull_resistor_1_node;
  wire [3:0] Estado_q, rom_1_data;

  ROM #(.dataWidth(19)) rom_1 (
    .addr({Instr[3:0], Estado_q}), .data({MEMrd, MEMwr, REGwr, Asel, Bsel, Csel, ALUop, rom_1_data}));
  Register #(.width(4)) Estado (.D(rom_1_data), .en(pull_resistor_1_node), .clk(clk), .Q(Estado_q), .clr(rst));
  Pull_Resistor #(.pull(1)) pull_resistor_1 (.node(pull_resistor_1_node));

  // Notes on the sheet:
  //   contents of rom_1 (hex, n*v repeats v):
  //   18121 58242 121a3 13*0 18121 58242 121a3 18124 58245 1a686
  //   Instr Atual MEMrd MEMwr REGwr Asel Bsel Csel ALUop Prox          Binário            HEXA
  //    0000  0000   0     0     1    100  000  010  010  0001   001.1000.0001.0010.0001  18121
  //    0000  0001   1     0     1    100  000  100  100  0010   101.1000.0010.0100.0010  58242
  //    0000  0010   0     0     1    001  000  011  010  0011   001.0010.0001.1010.0011  121a3
  //    0000  0011   0     0     0    000  000  000  000  0000   000.0000.0000.0000.0000  00000
  //    0001  0000   0     0     1    100  000  010  010  0001   001.1000.0001.0010.0001  18121
  //    0001  0001   1     0     1    100  000  100  100  0010   101.1000.0010.0100.0010  58242
  //    0001  0010   0     0     1    001  000  011  010  0011   001.0010.0001.1010.0011  121a3
  //    0001  0011   0     0     1    100  000  010  010  0100   001.1000.0001.0010.0100  18124
  //    0001  0100   1     0     1    100  000  100  100  0101   101.1000.0010.0100.0101  58245
  //    0001  0101   0     0     1    101  001  101  000  0110   001.1010.0110.1000.0110  1a686
  //   REGISTRADORES
  //     ZER0  000
  //     MDR   001
  //     MAR   010
  //     IR    011
  //     PC    100
  //     ACC   101
  //     AUX   110
  //     SP    111
  //     ALUop
  //   ADD   000
  //   AND   001
  //   OR    010
  //   NOT   011
  //   INC   100
  //   SRL   101
  //   SLL   110
  //   SRA   111
endmodule

module ALU (
  input  [7:0] Abus,
  input  [7:0] Bbus,
  input  [2:0] ALUop,
  output [7:0] Cbus,
  output [3:0] FLAGSout
);

  wire adder_1_cout, adder_2_cout;
  wire [6:0] adder_1_out;
  wire [7:0] and_1_out, multiplexer_1_out, not_1_out, or_1_out, shifter_1_out, shifter_2_out, shifter_3_out;
  wire [7:7] adder_2_out;

  Multiplexer #(.width(8)) multiplexer_1 (.in0(Bbus), .in1({8{1'b0}}), .out(multiplexer_1_out), .sel(ALUop[2]));
  Adder #(.width(7)) adder_1 (
    .a(Abus[6:0]), .b(multiplexer_1_out[6:0]), .out(adder_1_out), .cin(ALUop[2]), .cout(adder_1_cout));
  Adder #(.width(1)) adder_2 (
    .a(Abus[7]), .b(multiplexer_1_out[7]), .out(adder_2_out[7]), .cin(adder_1_cout), .cout(adder_2_cout));
  assign and_1_out = Abus & Bbus;  // AND_Gate and_1, 8 bits wide
  assign or_1_out = Abus | Bbus;  // OR_Gate or_1, 8 bits wide
  assign not_1_out = ~Abus;  // NOT_Gate not_1, 8 bits wide
  Shifter #(.shift("lr")) shifter_1 (.in(Abus), .\dist (3'b001), .out(shifter_1_out));
  Shifter shifter_2 (.in(Abus), .\dist (3'b001), .out(shifter_2_out));
  Shifter #(.shift("ar")) shifter_3 (.in(Abus), .\dist (3'b001), .out(shifter_3_out));
  xor xor_1 (FLAGSout[3], adder_1_cout, adder_2_cout);
  Multiplexer #(.select(3)) multiplexer_2 (
    .in0(adder_2_cout), .in1(1'b0), .in2(1'b0), .in3(1'b0), .in4(adder_2_cout), .in5(Abus[0]), .in6(Abus[7]),
    .in7(Abus[0]), .out(FLAGSout[2]), .sel(ALUop));
  Multiplexer #(.select(3), .width(8)) multiplexer_3 (
    .in0({adder_2_out[7], adder_1_out}), .in1(and_1_out), .in2(or_1_out), .in3(not_1_out),
    .in4({adder_2_out[7], adder_1_out}), .in5(shifter_1_out), .in6(shifter_2_out), .in7(shifter_3_out),
    .out(Cbus), .sel(ALUop));
  nor nor_1 (FLAGSout[1], Cbus[0], Cbus[1], Cbus[2], Cbus[3], Cbus[4], Cbus[5], Cbus[6], Cbus[7]);

  assign FLAGSout[0] = Cbus[7];

  // Other names for the same wires on the sheet: inc = ALUop[2]; N = Cbus[7]; Z = FLAGSout[1]; C = FLAGSout[2];
  //   V = FLAGSout[3]
endmodule
